// Digital circuit 32-bit_CLA.dig as structural Verilog
module _32_bit_CLA (
  input  [31:0] A,
  input  [31:0] B,
  input  C_in,
  output [31:0] S,
  output C_out
);

  wire _4_bit_cla_block_2_c_out, _4_bit_cla_block_3_c_out, _4_bit_cla_block_4_c_out,
       _4_bit_cla_block_5_c_out, _4_bit_cla_block_6_c_out, _4_bit_cla_block_7_c_out, _4_bit_cla_block_8_c_out;

  _4_bit_CLA_block _4_bit_cla_block_1 (
    .A(A[31:28]), .B(B[31:28]), .C_in(_4_bit_cla_block_2_c_out), .S(S[31:28]), .C_out(C_out));
  _4_bit_CLA_block _4_bit_cla_block_2 (
    .A(A[27:24]), .B(B[27:24]), .C_in(_4_bit_cla_block_3_c_out), .S(S[27:24]),
    .C_out(_4_bit_cla_block_2_c_out));
  _4_bit_CLA_block _4_bit_cla_block_3 (
    .A(A[23:20]), .B(B[23:20]), .C_in(_4_bit_cla_block_4_c_out), .S(S[23:20]),
    .C_out(_4_bit_cla_block_3_c_out));
  _4_bit_CLA_block _4_bit_cla_block_4 (
    .A(A[19:16]), .B(B[19:16]), .C_in(_4_bit_cla_block_5_c_out), .S(S[19:16]),
    .C_out(_4_bit_cla_block_4_c_out));
  _4_bit_CLA_block _4_bit_cla_block_5 (
    .A(A[15:12]), .B(B[15:12]), .C_in(_4_bit_cla_block_6_c_out), .S(S[15:12]),
    .C_out(_4_bit_cla_block_5_c_out));
  _4_bit_CLA_block _4_bit_cla_block_6 (
    .A(A[11:8]), .B(B[11:8]), .C_in(_4_bit_cla_block_7_c_out), .S(S[11:8]), .C_out(_4_bit_cla_block_6_c_out));
  _4_bit_CLA_block _4_bit_cla_block_7 (
    .A(A[7:4]), .B(B[7:4]), .C_in(_4_bit_cla_block_8_c_out), .S(S[7:4]), .C_out(_4_bit_cla_block_7_c_out));
  _4_bit_CLA_block _4_bit_cla_block_8 (
    .A(A[3:0]), .B(B[3:0]), .C_in(C_in), .S(S[3:0]), .C_out(_4_bit_cla_block_8_c_out));
endmodule
