// Digital circuit 4-bit_CLA_block.dig as structural Verilog
module _4_bit_CLA_block (
  input  [3:0] A,
  input  [3:0] B,
  input  C_in,
  output [3:0] S,
  output C_out
);

  wire add_2_c_o, add_3_c_o, add_4_c_o, and_1_out, and_2_out, and_3_out, and_4_out, and_5_out, and_6_out,
       and_7_out, and_8_out, and_9_out, or_2_out, or_3_out, or_4_out, or_5_out, or_6_out, or_7_out, or_8_out;

  or or_1 (C_out, and_1_out, or_2_out);
  and and_1 (and_1_out, C_in, and_4_out);
  or or_2 (or_2_out, and_2_out, and_6_out);
  and and_2 (and_2_out, or_3_out, or_5_out);
  Add add_1 (.a(A[3]), .b(B[3]), .c_i(add_2_c_o), .s(S[3]));  // open: c_o
  Add add_2 (.a(A[2]), .b(B[2]), .c_i(add_3_c_o), .s(S[2]), .c_o(add_2_c_o));
  or or_3 (or_3_out, and_3_out, and_7_out);
  and and_3 (and_3_out, or_4_out, or_6_out);
  Add add_3 (.a(A[1]), .b(B[1]), .c_i(add_4_c_o), .s(S[1]), .c_o(add_3_c_o));
  or or_4 (or_4_out, and_5_out, and_8_out);
  Add add_4 (.a(A[0]), .b(B[0]), .c_i(C_in), .s(S[0]), .c_o(add_4_c_o));
  and and_4 (and_4_out, or_8_out, or_7_out, or_6_out, or_5_out);
  and and_5 (and_5_out, and_9_out, or_7_out);
  or or_5 (or_5_out, B[3], A[3]);
  and and_6 (and_6_out, B[3], A[3]);
  or or_6 (or_6_out, B[2], A[2]);
  and and_7 (and_7_out, B[2], A[2]);
  or or_7 (or_7_out, B[1], A[1]);
  and and_8 (and_8_out, B[1], A[1]);
  and and_9 (and_9_out, B[0], A[0]);
  or or_8 (or_8_out, B[0], A[0]);

  // Notes on the sheet:
  //   P3
  //   G3
  //   P2
  //   G2
  //   P1
  //   G1
  //   G0
  //   P0
endmodule
