// Digital circuit 4-bit_multiplier.dig as structural Verilog
module _4_bit_multiplier (
  input  [3:0] B,
  input  [3:0] A,
  output [7:0] Prod
);

  wire add_2_c_o, add_2_s, add_3_c_o, add_3_s, add_4_c_o, add_5_c_o, add_5_s, add_6_c_o, add_6_s, add_7_c_o,
       add_8_c_o, add_8_s, add_9_c_o, add_10_c_o, add_10_s, add_11_c_o, add_12_c_o, and_1_out, and_2_out,
       and_3_out, and_4_out, and_5_out, and_6_out, and_7_out, and_8_out, and_9_out, and_10_out, and_11_out,
       and_12_out, and_13_out, and_14_out, and_16_out;

  and and_1 (and_1_out, B[3], A[3]);
  Add add_1 (.a(and_1_out), .b(add_2_c_o), .c_i(add_4_c_o), .s(Prod[6]), .c_o(Prod[7]));
  and and_2 (and_2_out, B[2], A[3]);
  Add add_2 (.a(and_2_out), .b(add_3_c_o), .c_i(add_5_c_o), .s(add_2_s), .c_o(add_2_c_o));
  and and_3 (and_3_out, B[1], A[3]);
  Add add_3 (.a(and_3_out), .b(add_6_c_o), .c_i(1'b0), .s(add_3_s), .c_o(add_3_c_o));
  and and_4 (and_4_out, B[3], A[2]);
  Add add_4 (.a(and_4_out), .b(add_2_s), .c_i(add_7_c_o), .s(Prod[5]), .c_o(add_4_c_o));
  and and_5 (and_5_out, B[0], A[3]);
  and and_6 (and_6_out, B[2], A[2]);
  Add add_5 (.a(and_6_out), .b(add_3_s), .c_i(add_8_c_o), .s(add_5_s), .c_o(add_5_c_o));
  and and_7 (and_7_out, B[1], A[2]);
  Add add_6 (.a(and_7_out), .b(and_5_out), .c_i(add_10_c_o), .s(add_6_s), .c_o(add_6_c_o));
  and and_8 (and_8_out, B[3], A[1]);
  Add add_7 (.a(and_8_out), .b(add_5_s), .c_i(add_9_c_o), .s(Prod[4]), .c_o(add_7_c_o));
  and and_9 (and_9_out, B[0], A[2]);
  and and_10 (and_10_out, B[2], A[1]);
  Add add_8 (.a(and_10_out), .b(add_6_s), .c_i(add_11_c_o), .s(add_8_s), .c_o(add_8_c_o));
  Add add_9 (.a(and_13_out), .b(add_8_s), .c_i(1'b0), .s(Prod[3]), .c_o(add_9_c_o));
  and and_11 (and_11_out, B[0], A[1]);
  and and_12 (and_12_out, B[1], A[1]);
  Add add_10 (.a(and_12_out), .b(and_9_out), .c_i(add_12_c_o), .s(add_10_s), .c_o(add_10_c_o));
  Add add_11 (.a(and_14_out), .b(add_10_s), .c_i(1'b0), .s(Prod[2]), .c_o(add_11_c_o));
  and and_13 (and_13_out, B[3], A[0]);
  Add add_12 (.a(and_16_out), .b(and_11_out), .c_i(1'b0), .s(Prod[1]), .c_o(add_12_c_o));
  and and_14 (and_14_out, B[2], A[0]);
  and and_15 (Prod[0], B[0], A[0]);
  and and_16 (and_16_out, B[1], A[0]);
endmodule
