// Digital circuit DMUX.dig as structural Verilog
module DMUX (
  input  [15:0] INST,
  output [1:0] DMUX
);

  wire LDR, nor_1_out, nor_2_out, not_1_out, not_2_out, or_2_out, or_3_out, or_4_out, SETH, Z;
  wire [2:0] or_1_out;

  zero_comparator zero_comparator_1 (.INST(INST), .Z(Z));
  assign or_1_out = INST[10:8] | INST[6:4] | INST[2:0];  // Or or_1, 3 bits wide
  or or_2 (or_2_out, INST[3], or_1_out[0], or_1_out[1], or_1_out[2], INST[7]);
  not not_1 (not_1_out, or_2_out);
  Decoder #(.Selector_Bits(4)) decoder_1 (
    .sel(INST[15:12]), .out_1(SETH), .out_5(LDR));  // open: out_0, out_2, out_3, out_4, out_6, out_7, out_8, out_9, out_10, out_11, out_12, out_13, out_14, out_15
  nor nor_1 (nor_1_out, not_1_out, LDR);
  or or_3 (or_3_out, Z, INST[15]);
  nor nor_2 (nor_2_out, INST[15], not_2_out);
  not not_2 (not_2_out, nor_1_out);
  or or_4 (or_4_out, nor_2_out, Z);
  PriorityEncoder #(.Selector_Bits(2)) priorityencoder_1 (
    .in0(or_3_out), .in1(LDR), .in2(or_4_out), .in3(SETH), .num(DMUX));  // open: any

  // Other names for the same wires on the sheet: _3 = INST[3]; _7 = INST[7]; opcode[3:0] = INST[15:12]

  // Notes on the sheet:
  //   Z
  //   Rd
  //   Ra
  //   Rb
  //   opcode
endmodule
