// Digital circuit alu_extn.dig as structural Verilog
module alu_extn (
  input  [15:0] A,
  input  [15:0] B,
  input  [2:0] ALUOP,
  output [15:0] RESULT,
  output [3:0] FLAG,
  output [15:0] R
);

  wire and_2_out, and_3_out, array_divider_1_v, c_out_add, c_outsub, comparator_1_lt, comparator_2_gt,
       multiply_1_v, or_1_out, or_2_out, zero_comparator_1_z, zero_comparator_2_z;
  wire [15:0] and_1_out, array_divider_1_q, array_divider_1_r, circular_shift_1_b, cla_1_s, cla_2_s,
       logical_shift_1_out, multiplexer_1_out, multiplexer_2_out, multiplexer_4_out, multiplexer_5_out,
       multiply_1_p, not_1_out, xor_1_out;
  wire [31:16] multiply_1_p_2;

  assign not_1_out = ~B;  // Not not_1, 16 bits wide
  zero_comparator zero_comparator_1 (.INST(A), .Z(zero_comparator_1_z));
  zero_comparator zero_comparator_2 (.INST(B), .Z(zero_comparator_2_z));
  Comparator #(.Bits(16)) comparator_1 (.a(A), .b(B), .lt(comparator_1_lt));  // open: gt, eq
  Comparator #(.Bits(16)) comparator_2 (.a(A), .b(B), .gt(comparator_2_gt));  // open: eq, lt
  CLA cla_1 (.A(A), .B(B), .C_in(1'b0), .S(cla_1_s), .C_out(c_out_add));
  CLA cla_2 (.A(A), .B(not_1_out), .C_in(1'b1), .S(cla_2_s), .C_out(c_outsub));
  assign and_1_out = A & B;  // And and_1, 16 bits wide
  assign xor_1_out = A ^ B;  // XOr xor_1, 16 bits wide
  circular_shift circular_shift_1 (.A(A), .shift(B[3:0]), .B(circular_shift_1_b));
  multiply multiply_1 (.A(A), .B(B), .P({multiply_1_p_2, multiply_1_p}), .V(multiply_1_v));
  logical_shift logical_shift_1 (.A(A), .shift(B[3:0]), .OUT(logical_shift_1_out));
  array_divider array_divider_1 (.A(A), .B(B), .Q(array_divider_1_q), .R(array_divider_1_r), .V(array_divider_1_v));
  or or_1 (or_1_out, zero_comparator_1_z, zero_comparator_2_z);
  and and_2 (and_2_out, A[15], B[15]);
  or or_2 (or_2_out, or_1_out, comparator_1_lt);
  and and_3 (and_3_out, comparator_2_gt, and_2_out);
  Multiplexer #(.Bits(16)) multiplexer_1 (
    .sel(or_2_out), .in_0(multiplexer_2_out), .in_1({16{1'b0}}), .out(multiplexer_1_out));
  Multiplexer #(.Bits(16)) multiplexer_2 (
    .sel(and_3_out), .in_0(array_divider_1_q), .in_1(16'h1), .out(multiplexer_2_out));
  Multiplexer #(.Selector_Bits(3), .Bits(16)) multiplexer_3 (
    .sel(ALUOP), .in_0(cla_1_s), .in_1(cla_2_s), .in_2(and_1_out), .in_3(xor_1_out),
    .in_4(circular_shift_1_b), .in_5(multiply_1_p), .in_6(logical_shift_1_out), .in_7(multiplexer_1_out),
    .out(RESULT));
  Multiplexer #(.Bits(16)) multiplexer_4 (
    .sel(comparator_1_lt), .in_0(multiplexer_5_out), .in_1(A), .out(multiplexer_4_out));
  Multiplexer #(.Bits(16)) multiplexer_5 (
    .sel(and_3_out), .in_0(array_divider_1_r), .in_1(cla_2_s), .out(multiplexer_5_out));
  flags_setter flags_setter_1 (
    .RES(RESULT), .A(A), .B(B), .op(ALUOP), .IN(RESULT), .Carry_add(c_out_add), .Carry_sub(c_outsub),
    .Mul_V(multiply_1_v), .R(multiplexer_4_out), .Div_V(array_divider_1_v), .Z(FLAG[0]), .N(FLAG[1]),
    .C(FLAG[2]), .V(FLAG[3]), .REM(R));

  // Other names for the same wires on the sheet: op[2:0] = ALUOP

  // Notes on the sheet:
  //   A: First input to ALU
  //   B: Second input to ALU
  //   RESULT: The result of this ALU operation
  //   FLAG: The flags associated with the result of this ALU operation
  //   0. Z (zero)
  //   1. N (negative)
  //   2. C (carry)
  //   3. V (overflow)
  //   ALUOP: Operation selection input
  //   R: Remainder from division
endmodule

/* Test case RESULT:
ALUOP A B RESULT

# Test small results
loop(a, 1 << 4)
loop(b, 1 << 4)
    (0) (a) (b) ((a + b) & 0xFFFF)
    (1) (a) (b) ((a - b) & 0xFFFF)
    (2) (a) (b) (a & b)
    (3) (a) (b) (a ^ b)
    #(4) (a) (b) (a >> b)
    (5) (a) (b) ((a * b) & 0xFFFF)
    (6) (a) (b) (a << b)

end loop
end loop


# Test large results
loop(i, 1000)
    let a = random(1 << 16);
    let b = random(1 << 16);
    let shift = random(1 << 4);

    (0) (a) (b) ((a + b) & 0xFFFF)
    (1) (a) (b) ((a - b) & 0xFFFF)
    (2) (a) (b) (a & b)
    (3) (a) (b) (a ^ b)
    #(4) (a) (b) (a >> b)
    (5) (a) (b) ((a * b) & 0xFFFF)
    (6) (a) (shift) (a << shift)

end loop
*/

/* Test case Z:
ALUOP A B Z

declare Z = FLAG & 0b1;

# Test all zero cases
00 0 0 1
01 0 0 1
10 0 0 1
11 0 0 1

# Test 1 + (-1) = 0
00 1 0xFFFF 1

# Test with a single bit set in A
loop(s, 16)
    let a = 1 << s;

    00 (a) 0 (a = 0)
    01 (a) 0 (a = 0)
    10 (a) 0 1
    11 (a) 0 (a = 0)
end loop

# Test random inputs
loop(i, 200)
    let a = random(1 << 16);
    let b = random(1 << 16);

    00 (a) (b) (((a + b) & 0xFFFF) = 0)
    01 (a) (b) (((a - b) & 0xFFFF) = 0)
    10 (a) (b) ((a & b) = 0)
    11 (a) (b) ((a ^ b) = 0)
end loop
*/

/* Test case N:
ALUOP A B N

declare N = (FLAG >> 1) & 0b1;

# Test all zero cases
00 0 0 0
01 0 0 0
10 0 0 0
11 0 0 0

00 1 0xFFFF 0

# Test with a single bit set in A
loop(s, 16)
    let a = 1 << s;

    00 (a) 0 ((a >> 15) & 0b1)
    01 (a) 0 ((a >> 15) & 0b1)
    10 (a) 0 0
    11 (a) 0 ((a >> 15) & 0b1)
end loop

# Test random inputs
loop(i, 200)
    let a = random(1 << 16);
    let b = random(1 << 16);

    00 (a) (b) (((a + b) >> 15) & 0b1)
    01 (a) (b) (((a - b) >> 15) & 0b1)
    10 (a) (b) (((a & b) >> 15) & 0b1)
    11 (a) (b) (((a ^ b) >> 15) & 0b1)
end loop
*/

/* Test case C:
ALUOP A B C

declare C = (FLAG >> 2) & 0b1;

00 0 0 0

# (0 - 0) is implemented as 0 + (0xFFFF + 1), so a carry is expected
01 0 0 1

# Carry should propagate all the way from the first bit if necessary
00 1 0xFFFF 1

# Test with a single bit set in A
loop(s, 16)
    let a = 1 << s;

    00 (a) 0 0
    01 (a) 0 1  # (a - 0) is implemented as (a + 0xFFFF + 1) in the adder, so a carry is always expected
    10 (a) 0 0  # carry is defined as 0 for AND
    11 (a) 0 0  # carry is defined as 0 for XOR
end loop

# Adding 15 bit values should never carry
loop(i, 100)
    00 (random(1 << 15)) (random(1 << 15)) 0
end loop

# Test random inputs
loop(i, 200)
    let a = random(1 << 16);
    let b = random(1 << 16);

    00 (a) (b) (((a + b) >> 16) & 0b1)
    01 (a) (b) (~((a - b) >> 16) & 0b1)
end loop

# AND and XOR never set carry
loop(i, 100)
    let a = random(1 << 16);
    let b = random(1 << 16);
    10 (a) (b) 0
    11 (a) (b) 0
end loop
*/

/* Test case V:
ALUOP A B V

declare V = (FLAG >> 3) & 0b1;

00 0 0 0
01 0 0 0

# 1 + (-1) = 0  ; different input signs = no overflow here!
00 1 0xFFFF 0

# 3 - 5 = 3 + (-5) = -2  ; subtraction inverts the second operand sign
01 3 5 0

# Some edge cases when subtracting 0x8000
01 0x8000 0x8000 0
01 0xFFFF 0x8000 0
01 0x7FFF 0x8000 1

# Test with a single bit set in A
loop(s, 16)
    let a = 1 << s;

    00 (a) 0 0
    01 (a) 0 0
    10 (a) 0 0  # overflow is defined as 0 for AND
    11 (a) 0 0  # overflow is defined as 0 for XOR
end loop

# Test random inputs
loop(i, 200)
    let a = random(1 << 16);
    let b = random(1 << 16);

    00 (a) (b) (((~(a ^ b) & (a ^ (a + b))) >> 15) & 0b1)
    01 (a) (b) (((~(a ^ -b) & (a ^ (a - b))) >> 15) & 0b1)
end loop

# AND and XOR never set overflow
loop(i, 100)
    let a = random(1 << 16);
    let b = random(1 << 16);
    10 (a) (b) 0
    11 (a) (b) 0
end loop
*/

/* Test case DIV:
ALUOP A B RESULT R
loop(i, 100)
	let ALUOP = 7;
    	let A = random(1 << 16);
    	let B = random(1 << 16);

	(ALUOP) (A) (B) ((A/B) & 0xffff) ((-(A/B)*B)+A)
end loop
*/

/* Test case MULT:
ALUOP A B RESULT

# Test small results
loop(a, 1 << 4)
loop(b, 1 << 4)

    (5) (a) (b) ((a * b) & 0xFFFF)

end loop
end loop


# Test large results
loop(i, 1000)
    let a = random(1 << 16);
    let b = random(1 << 16);

    (5) (a) (b) ((a * b) & 0xFFFF)

end loop
*/

/* Test case Logical Shift Left:
ALUOP A B RESULT

# Test small results
loop(a, 1 << 4)
loop(b, 1 << 4)

    (6) (a) (b) (a << b)

end loop
end loop


# Test large results
loop(i, 1000)
    let a = random(1 << 16);
    let b = random(1 << 4);

    (6) (a) (b) (a << b)

end loop
*/
