// Digital circuit circular_shift.dig as structural Verilog
module circular_shift (
  input  [15:0] A,
  input  [3:0] shift,
  output [15:0] B
);

  Multiplexer #(.Selector_Bits(4)) multiplexer_1 (
    .sel(shift), .in_0(A[0]), .in_1(A[1]), .in_2(A[2]), .in_3(A[3]), .in_4(A[4]), .in_5(A[5]), .in_6(A[6]),
    .in_7(A[7]), .in_8(A[8]), .in_9(A[9]), .in_10(A[10]), .in_11(A[11]), .in_12(A[12]), .in_13(A[13]),
    .in_14(A[14]), .in_15(A[15]), .out(B[0]));
  Multiplexer #(.Selector_Bits(4)) multiplexer_2 (
    .sel(shift), .in_0(A[12]), .in_1(A[13]), .in_2(A[14]), .in_3(A[15]), .in_4(A[0]), .in_5(A[1]),
    .in_6(A[2]), .in_7(A[3]), .in_8(A[4]), .in_9(A[5]), .in_10(A[6]), .in_11(A[7]), .in_12(A[8]),
    .in_13(A[9]), .in_14(A[10]), .in_15(A[11]), .out(B[12]));
  Multiplexer #(.Selector_Bits(4)) multiplexer_3 (
    .sel(shift), .in_0(A[8]), .in_1(A[9]), .in_2(A[10]), .in_3(A[11]), .in_4(A[12]), .in_5(A[13]),
    .in_6(A[14]), .in_7(A[15]), .in_8(A[0]), .in_9(A[1]), .in_10(A[2]), .in_11(A[3]), .in_12(A[4]),
    .in_13(A[5]), .in_14(A[6]), .in_15(A[7]), .out(B[8]));
  Multiplexer #(.Selector_Bits(4)) multiplexer_4 (
    .sel(shift), .in_0(A[4]), .in_1(A[5]), .in_2(A[6]), .in_3(A[7]), .in_4(A[8]), .in_5(A[9]), .in_6(A[10]),
    .in_7(A[11]), .in_8(A[12]), .in_9(A[13]), .in_10(A[14]), .in_11(A[15]), .in_12(A[0]), .in_13(A[1]),
    .in_14(A[2]), .in_15(A[3]), .out(B[4]));
  Multiplexer #(.Selector_Bits(4)) multiplexer_5 (
    .sel(shift), .in_0(A[15]), .in_1(A[0]), .in_2(A[1]), .in_3(A[2]), .in_4(A[3]), .in_5(A[4]), .in_6(A[5]),
    .in_7(A[6]), .in_8(A[7]), .in_9(A[8]), .in_10(A[9]), .in_11(A[10]), .in_12(A[11]), .in_13(A[12]),
    .in_14(A[13]), .in_15(A[14]), .out(B[15]));
  Multiplexer #(.Selector_Bits(4)) multiplexer_6 (
    .sel(shift), .in_0(A[11]), .in_1(A[12]), .in_2(A[13]), .in_3(A[14]), .in_4(A[15]), .in_5(A[0]),
    .in_6(A[1]), .in_7(A[2]), .in_8(A[3]), .in_9(A[4]), .in_10(A[5]), .in_11(A[6]), .in_12(A[7]),
    .in_13(A[8]), .in_14(A[9]), .in_15(A[10]), .out(B[11]));
  Multiplexer #(.Selector_Bits(4)) multiplexer_7 (
    .sel(shift), .in_0(A[7]), .in_1(A[8]), .in_2(A[9]), .in_3(A[10]), .in_4(A[11]), .in_5(A[12]),
    .in_6(A[13]), .in_7(A[14]), .in_8(A[15]), .in_9(A[0]), .in_10(A[1]), .in_11(A[2]), .in_12(A[3]),
    .in_13(A[4]), .in_14(A[5]), .in_15(A[6]), .out(B[7]));
  Multiplexer #(.Selector_Bits(4)) multiplexer_8 (
    .sel(shift), .in_0(A[3]), .in_1(A[4]), .in_2(A[5]), .in_3(A[6]), .in_4(A[7]), .in_5(A[8]), .in_6(A[9]),
    .in_7(A[10]), .in_8(A[11]), .in_9(A[12]), .in_10(A[13]), .in_11(A[14]), .in_12(A[15]), .in_13(A[0]),
    .in_14(A[1]), .in_15(A[2]), .out(B[3]));
  Multiplexer #(.Selector_Bits(4)) multiplexer_9 (
    .sel(shift), .in_0(A[14]), .in_1(A[15]), .in_2(A[0]), .in_3(A[1]), .in_4(A[2]), .in_5(A[3]), .in_6(A[4]),
    .in_7(A[5]), .in_8(A[6]), .in_9(A[7]), .in_10(A[8]), .in_11(A[9]), .in_12(A[10]), .in_13(A[11]),
    .in_14(A[12]), .in_15(A[13]), .out(B[14]));
  Multiplexer #(.Selector_Bits(4)) multiplexer_10 (
    .sel(shift), .in_0(A[10]), .in_1(A[11]), .in_2(A[12]), .in_3(A[13]), .in_4(A[14]), .in_5(A[15]),
    .in_6(A[0]), .in_7(A[1]), .in_8(A[2]), .in_9(A[3]), .in_10(A[4]), .in_11(A[5]), .in_12(A[6]),
    .in_13(A[7]), .in_14(A[8]), .in_15(A[9]), .out(B[10]));
  Multiplexer #(.Selector_Bits(4)) multiplexer_11 (
    .sel(shift), .in_0(A[6]), .in_1(A[7]), .in_2(A[8]), .in_3(A[9]), .in_4(A[10]), .in_5(A[11]),
    .in_6(A[12]), .in_7(A[13]), .in_8(A[14]), .in_9(A[15]), .in_10(A[0]), .in_11(A[1]), .in_12(A[2]),
    .in_13(A[3]), .in_14(A[4]), .in_15(A[5]), .out(B[6]));
  Multiplexer #(.Selector_Bits(4)) multiplexer_12 (
    .sel(shift), .in_0(A[2]), .in_1(A[3]), .in_2(A[4]), .in_3(A[5]), .in_4(A[6]), .in_5(A[7]), .in_6(A[8]),
    .in_7(A[9]), .in_8(A[10]), .in_9(A[11]), .in_10(A[12]), .in_11(A[13]), .in_12(A[14]), .in_13(A[15]),
    .in_14(A[0]), .in_15(A[1]), .out(B[2]));
  Multiplexer #(.Selector_Bits(4)) multiplexer_13 (
    .sel(shift), .in_0(A[13]), .in_1(A[14]), .in_2(A[15]), .in_3(A[0]), .in_4(A[1]), .in_5(A[2]),
    .in_6(A[3]), .in_7(A[4]), .in_8(A[5]), .in_9(A[6]), .in_10(A[7]), .in_11(A[8]), .in_12(A[9]),
    .in_13(A[10]), .in_14(A[11]), .in_15(A[12]), .out(B[13]));
  Multiplexer #(.Selector_Bits(4)) multiplexer_14 (
    .sel(shift), .in_0(A[9]), .in_1(A[10]), .in_2(A[11]), .in_3(A[12]), .in_4(A[13]), .in_5(A[14]),
    .in_6(A[15]), .in_7(A[0]), .in_8(A[1]), .in_9(A[2]), .in_10(A[3]), .in_11(A[4]), .in_12(A[5]),
    .in_13(A[6]), .in_14(A[7]), .in_15(A[8]), .out(B[9]));
  Multiplexer #(.Selector_Bits(4)) multiplexer_15 (
    .sel(shift), .in_0(A[5]), .in_1(A[6]), .in_2(A[7]), .in_3(A[8]), .in_4(A[9]), .in_5(A[10]), .in_6(A[11]),
    .in_7(A[12]), .in_8(A[13]), .in_9(A[14]), .in_10(A[15]), .in_11(A[0]), .in_12(A[1]), .in_13(A[2]),
    .in_14(A[3]), .in_15(A[4]), .out(B[5]));
  Multiplexer #(.Selector_Bits(4)) multiplexer_16 (
    .sel(shift), .in_0(A[1]), .in_1(A[2]), .in_2(A[3]), .in_3(A[4]), .in_4(A[5]), .in_5(A[6]), .in_6(A[7]),
    .in_7(A[8]), .in_8(A[9]), .in_9(A[10]), .in_10(A[11]), .in_11(A[12]), .in_12(A[13]), .in_13(A[14]),
    .in_14(A[15]), .in_15(A[0]), .out(B[1]));

  // Other names for the same wires on the sheet: _0 = B[0]; _1 = B[15]; _2 = B[14]; _3 = B[13]; _4 = B[12];
  //   _5 = B[11]; _6 = B[10]; _7 = B[9]; _8 = B[8]; _9 = B[7]; _10 = B[6]; _11 = B[5]; _12 = B[4]; _13 = B[3];
  //   _14 = B[2]; _15 = B[1]
endmodule
