// Digital circuit condition_check.dig as structural Verilog
module condition_check (
  input  COND,
  input  Z,
  output EXEC
);

  wire and_1_out, not_1_out;

  not not_1 (not_1_out, COND);
  and and_1 (and_1_out, COND, Z);
  or or_1 (EXEC, not_1_out, and_1_out);
endmodule
