// Digital circuit control_unit_extn.dig as structural Verilog
module control_unit_extn (
  input  [15:0] INST,
  input  [15:0] FLAG,
  input  CLK,
  output [2:0] RS1,
  output [2:0] RS2,
  output [2:0] WS,
  output [1:0] DMUX,
  output PC_write,
  output EXEC,
  output [2:0] ALUOP,
  output STR,
  output LDR,
  output WE,
  output FLEN,
  output REM_en,
  output [2:0] WS2,
  output [2:0] RS3,
  output POST_addr,
  output SHADOW_en
);

  wire decoder_1_out_6, main_decoder_1_ldrr, main_decoder_1_strr, or_1_out;

  condition_check condition_check_1 (.COND(INST[11]), .Z(FLAG[0]), .EXEC(EXEC));
  Multiplexer #(.Bits(3)) multiplexer_1 (.sel(POST_addr), .in_0(INST[10:8]), .in_1(INST[6:4]), .out(WS));
  Multiplexer #(.Bits(3)) multiplexer_2 (.sel(or_1_out), .in_0(INST[2:0]), .in_1(INST[10:8]), .out(RS2));
  Multiplexer #(.Bits(3)) multiplexer_3 (.sel(or_1_out), .in_0(INST[10:8]), .in_1(INST[2:0]), .out(RS3));
  main_decoder main_decoder_1 (
    .opcode(INST[15:12]), .EXEC(EXEC), .CLK(CLK), .ALUOP(ALUOP), .STR(STR), .WE(WE), .LDR(LDR), .FLEN(FLEN),
    .DIV(REM_en), .STRR(main_decoder_1_strr), .LDRR(main_decoder_1_ldrr), .SHADOW_en(SHADOW_en));
  Decoder #(.Selector_Bits(3)) decoder_1 (
    .sel(INST[10:8]), .out_6(decoder_1_out_6));  // open: out_0, out_1, out_2, out_3, out_4, out_5, out_7
  or or_1 (or_1_out, main_decoder_1_ldrr, main_decoder_1_strr, LDR, STR);
  DMUX dmux_1 (.INST(INST), .DMUX(DMUX));
  or or_2 (POST_addr, main_decoder_1_strr, main_decoder_1_ldrr);
  and and_1 (PC_write, EXEC, decoder_1_out_6);

  assign RS1 = INST[6:4];
  assign WS2 = INST[10:8];

  // Other names for the same wires on the sheet: _3 = INST[3]; _7 = INST[7]; rd[2:0] = INST[10:8]; post = POST_addr

  // Notes on the sheet:
  //   Rd
  //   Ra
  //   cond
  //   opcode
  //   Rb
endmodule

/* Test case ALUOP:
	INST                                    ALUOP 

let aluop  = 0b1000;
let ldrop  = 0b0101;
let strop  = 0b0100;
let movlop = 0b0000;

loop(rd, 1<<3)
loop(ra, 1<<3)
loop(rb, 1<<3)

loop(i, 4)
	((aluop+i)<<12 | rd<<8 | ra<<4 | rb<<0) (i)    #test add/sub/and/xor
end loop

end loop
end loop
end loop
*/

/* Test case WS:
	INST                                    WS 

let aluop  = 0b1000;
let ldrop  = 0b0101;
let strop  = 0b0100;
let movlop = 0b0000;

loop(rd, 1<<3)
loop(ra, 1<<3)
loop(rb, 1<<3)

loop(i, 4)
	((aluop+i)<<12 | rd<<8 | ra<<4 | rb<<0) (rd)  #test add/sub/and/xor
end loop

	(ldrop    <<12 | rd<<8 | ra<<4 )        (rd)   #test ldr
	(strop    <<12 | rd<<8 | ra<<4 )        X     #test str
	
	let imm = random(256);
	(movlop   <<12 | rd<<8 | imm )          (rd)  #test movl

end loop
end loop
end loop
*/

/* Test case RS2:
	INST                                    RS2  

let aluop  = 0b1000;
let ldrop  = 0b0101;
let strop  = 0b0100;
let movlop = 0b0000;

loop(rd, 1<<3)
loop(ra, 1<<3)
loop(rb, 1<<3)

loop(i, 4)
	((aluop+i)<<12 | rd<<8 | ra<<4 | rb<<0) (rb) #test add/sub/and/xor
end loop
	(strop    <<12 | rd<<8 | ra<<4 )        (rd) #test str

end loop
end loop
end loop
*/

/* Test case STR:
	INST                                    STR 

let aluop  = 0b1000;
let ldrop  = 0b0101;
let strop  = 0b0100;
let movlop = 0b0000;

loop(rd, 1<<3)
loop(ra, 1<<3)
loop(rb, 1<<3)

loop(i, 4)
	((aluop+i)<<12 | rd<<8 | ra<<4 | rb<<0) 0  #test add/sub/and/xor
end loop

	(ldrop    <<12 | rd<<8 | ra<<4 )        0  #test ldr
	(strop    <<12 | rd<<8 | ra<<4 )        1  #test str
	
	let imm = random(256);
	(movlop   <<12 | rd<<8 | imm )          0  #test movl

end loop
end loop
end loop
*/

/* Test case EXEC:
FLAG INST EXEC
0000 0b0000000000000000 1
0000 0b0000100000000000 0
0001 0b0000100000000000 1
0001 0b0000000000000000 1

1010 0b0000000000000000 1
0100 0b0000100000011111 0
1101 0b0000100000000000 1
0011 0b0100000111100010 1

1110 0b0110000000011100 1
1110 0b0000100000000000 0
1111 0b0000100000000000 1
1111 0b0000000000000000 1
*/

/* Test case All Tests:
	INST                                WE  ALUOP  RS1   RS2  WS  STR  LDR DMUX

let aluop  = 0b1000;
let ldrop  = 0b0101;
let strop  = 0b0100;
let movlop = 0b0000;
let sethop = 0b0001;

loop(rd, 1<<3)
loop(ra, 1<<3)
loop(rb, 1<<3)

loop(i, 4)
	((aluop+i)<<12 | rd<<8 | ra<<4 | rb<<0)  1  (i)     (ra)  (rb) (rd)  0   X    0  #test add/sub/and/xor
end loop

	(ldrop    <<12 | rd<<8 | ra<<4 )         1  X       (ra)  x    (rd)  0   1    1  #test ldr
	(strop    <<12 | rd<<8 | ra<<4 )         0  X       (ra)  (rd)  X    1   X    X  #test str
	
	let imm = random(256);
	(movlop   <<12 | rd<<8 | imm )           1  X       X      X   (rd)  0   X    2  #test movl

	let imm = random(256);
	(sethop   <<12 | rd<<8 | imm )           1  X       X      X   (rd)  0   X    3  #test seth

end loop
end loop
end loop
*/

/* Test case DMUX:
	INST                                    DMUX

let aluop  = 0b1000;
let ldrop  = 0b0101;
let strop  = 0b0100;
let movlop = 0b0000;
let sethop = 0b0001;

loop(rd, 1<<3)
loop(ra, 1<<3)
loop(rb, 1<<3)

loop(i, 4)
	((aluop+i)<<12 | rd<<8 | ra<<4 | rb<<0) 0  #test add/sub/and/xor
end loop

	(ldrop    <<12 | rd<<8 | ra<<4 )        1  #test ldr
	
	let imm = random(256);
	(movlop   <<12 | rd<<8 | imm )          2  #test movl

	let imm = random(256);
	(sethop   <<12 | rd<<8 | imm )          3  #test seth

end loop
end loop
end loop
*/

/* Test case WE:
	INST                                    WE  

let aluop  = 0b1000;
let ldrop  = 0b0101;
let strop  = 0b0100;
let strrop = 0b0110;
let ldrrop = 0b0111;
let movlop = 0b0000;

loop(rd, 1<<3)
loop(ra, 1<<3)
loop(rb, 1<<3)

loop(i, 4)
	((aluop+i)<<12 | rd<<8 | ra<<4 | rb<<0) 1  #test add/sub/and/xor
end loop

	(ldrop    <<12 | rd<<8 | ra<<4 )        1  #test ldr
	(strop    <<12 | rd<<8 | ra<<4 )        0  #test str
	(ldrrop    <<12 | rd<<8 | ra<<4 )        1  #test ldr
	(strrop    <<12 | rd<<8 | ra<<4 )        1  #test str
	
	let imm = random(256);
	(movlop   <<12 | rd<<8 | imm )          1  #test movl

end loop
end loop
end loop
*/

/* Test case RS1:
	INST                                    RS1  

let aluop  = 0b1000;
let ldrop  = 0b0101;
let strop  = 0b0100;
let movlop = 0b0000;

loop(rd, 1<<3)
loop(ra, 1<<3)
loop(rb, 1<<3)

loop(i, 4)
	((aluop+i)<<12 | rd<<8 | ra<<4 | rb<<0) (ra)  #test add/sub/and/xor
end loop

	(ldrop    <<12 | rd<<8 | ra<<4 )        (ra)  #test ldr
	(strop    <<12 | rd<<8 | ra<<4 )        (ra)  #test str

end loop
end loop
end loop
*/

/* Test case LDR:
	INST                                    LDR 

let aluop  = 0b1000;
let ldrop  = 0b0101;
let strop  = 0b0100;
let movlop = 0b0000;

loop(rd, 1<<3)
loop(ra, 1<<3)
loop(rb, 1<<3)

loop(i, 4)
	((aluop+i)<<12 | rd<<8 | ra<<4 | rb<<0) X    #test add/sub/and/xor
end loop

	(ldrop    <<12 | rd<<8 | ra<<4 )        1    #test ldr
	(strop    <<12 | rd<<8 | ra<<4 )        X    #test str
	
	let imm = random(256);
	(movlop   <<12 | rd<<8 | imm )          X    #test movl

end loop
end loop
end loop
*/

/* Test case FLEN:
INST                FLEN
0b1000000000000000   1
0b1001000000000000   1
0b1010000000000000   1
0b1011000000000000   1
X                    0
*/
