// Digital circuit counter.dig as structural Verilog
module counter (
  input  [15:0] PC,
  output [15:0] Q
);

  Add #(.Bits(16)) plus_1 (.a(16'h1), .b(PC), .c_i(1'b0), .s(Q));  // open: c_o
endmodule
