// Digital circuit divide_logic.dig as structural Verilog
module divide_logic (
  input  B,
  input  R_2,
  input  C_in,
  input  N,
  output R,
  output C_out,
  output D
);

  Multiplexer multiplexer_1 (.sel(N), .in_0(D), .in_1(R_2), .out(R));
  Add add_1 (.a(R_2), .b(B), .c_i(C_in), .s(D), .c_o(C_out));
endmodule
