// Digital circuit extended-cpu.dig as structural Verilog
module extended_cpu (
  input  CLK
);

  wire EXEC, FLEN, LDR, PC_write, POST_addr, REM_en, SHADOW_en, STR, WE;
  wire [1:0] DMUX;
  wire [2:0] ALUOP, RS1, RS2, RS3, WS, WS2;
  wire [3:0] alu_extn_1_flag;
  wire [15:0] alu_extn_1_r, alu_extn_1_result, FLAG, imm8_extender_1_imm8, multiplexer_1_out,
       multiplexer_2_out, multiplexer_3_out, multiplexer_4_out, multiplexer_5_out, multiplexer_6_out,
       neg_1_out, pre_post_addr_1__1a, RAM_d1, RAM_d2, reg_file_extn_1_fl, reg_file_extn_1_out1,
       reg_file_extn_1_out2, reg_file_extn_1_pc, seth_1_p2, seth_1_p3;

  LED u_EXEC (.in(EXEC));
  RAMDualAccess #(.AddrBits(16), .isProgramMemory("true"), .Bits(16)) RAM (
    .str(STR), .C(CLK), .ld(LDR), .A1(pre_post_addr_1__1a), .Din1(reg_file_extn_1_out2),
    .A2(reg_file_extn_1_pc), .D1(RAM_d1), .D2(RAM_d2));
  pre_post_addr pre_post_addr_1 (.RA(reg_file_extn_1_out1), .RB(seth_1_p3), .en(POST_addr), ._1A(pre_post_addr_1__1a));
  imm8_extender imm8_extender_1 (.INST(RAM_d2), .IMM8(imm8_extender_1_imm8));
  control_unit_extn control_unit_extn_1 (
    .INST(RAM_d2), .FLAG(reg_file_extn_1_fl), .CLK(CLK), .RS1(RS1), .RS2(RS2), .WS(WS), .DMUX(DMUX),
    .PC_write(PC_write), .EXEC(EXEC), .ALUOP(ALUOP), .STR(STR), .LDR(LDR), .WE(WE), .FLEN(FLEN),
    .REM_en(REM_en), .WS2(WS2), .RS3(RS3), .POST_addr(POST_addr), .SHADOW_en(SHADOW_en));
  Multiplexer #(.Bits(16)) multiplexer_1 (
    .sel(RAM_d2[13]), .in_0(imm8_extender_1_imm8), .in_1(neg_1_out), .out(multiplexer_1_out));
  Neg #(.Bits(16)) neg_1 (.in(imm8_extender_1_imm8), .out(neg_1_out));
  // seth seth_1: pin names not known; wires that end beside it: imm8_extender_1_imm8, seth_1_p2, seth_1_p3
  Multiplexer #(.Bits(16)) multiplexer_2 (
    .sel(POST_addr), .in_0(multiplexer_1_out), .in_1(RAM_d1), .out(multiplexer_2_out));
  Multiplexer #(.Selector_Bits(2), .Bits(16)) multiplexer_3 (
    .sel(DMUX), .in_0(alu_extn_1_result), .in_1(RAM_d1), .in_2(multiplexer_2_out), .in_3(seth_1_p2),
    .out(multiplexer_3_out));
  Multiplexer #(.Selector_Bits(2), .Bits(16)) multiplexer_4 (
    .sel(DMUX), .in_0(alu_extn_1_result), .in_1(RAM_d1), .in_2(multiplexer_2_out), .in_3(seth_1_p2),
    .out(multiplexer_4_out));
  Multiplexer #(.Bits(16)) multiplexer_5 (
    .sel(POST_addr), .in_0(multiplexer_3_out), .in_1(alu_extn_1_result), .out(multiplexer_5_out));
  reg_file_extn reg_file_extn_1 (
    .RS1(RS1), .RS2(RS2), .WS1(WS), .WE(WE), .D_IN1(multiplexer_5_out), .CLK(CLK), .FLAG(FLAG), .FLEN(FLEN),
    .WS2(WS2), .D_IN2(multiplexer_4_out), .RS3(RS3), .SHADOW_en(SHADOW_en), .OUT1(reg_file_extn_1_out1),
    .OUT2(reg_file_extn_1_out2), .PC(reg_file_extn_1_pc), .OUT3(seth_1_p3), .FL(reg_file_extn_1_fl));
  alu_extn alu_extn_1 (
    .A(reg_file_extn_1_out1), .B(multiplexer_6_out), .ALUOP(ALUOP), .RESULT(alu_extn_1_result),
    .FLAG(alu_extn_1_flag), .R(alu_extn_1_r));
  Multiplexer #(.Bits(16)) multiplexer_6 (
    .sel(POST_addr), .in_0(reg_file_extn_1_out2), .in_1(seth_1_p3), .out(multiplexer_6_out));
  _4_16_extender _4_16_extender_1 (.IN(alu_extn_1_flag), .OUT(FLAG));
  Register #(.Bits(16)) REM (.D(alu_extn_1_r), .C(CLK), .en(REM_en));  // open: Q
endmodule

/* Test case DIV:
CLK     R1     R2     R3     R4   REM   PC

0        x      x      x      x     x   0x0000
c   0x0005      x      x      x     x   0x0001
c   0x0005 0x0003      x      x     x   0x0002
c   0x0005 0x0003 0x0001      x     2   0x0003
c   0x0006 0x0003 0x0001      x     2   0x0004
c   0x0006 0x0003 0x0002      x     0   0x0005
c   0x0037 0x0003 0x0002      x     0   0x0006
c   0x0037 0x0005 0x0002      x     0   0x0007
c   0x0037 0x0005 0x000B      x     0   0x0008
c   0x0037 0x0004 0x000B      x     0   0x0009
c   0x0037 0x0004 0x000B 0x000D     3   0x000A
c   0x0080 0x0004 0x000B 0x000D     3   0x000B
c   0x0080 0x0004 0x0010 0x000D     3   0x000C
c   0x0080 0x0008 0x0010 0x000D     0   0x000D

program(0x0105, 0x0203, 0xF312, 0x0106, 0xF312, 0x0137, 0x0205, 0xF312, 0x0204, 0xF412, 0x0180, 0x0310, 0xF213)
*/

/* Test case LSL:
CLK     R1     R2     R3     R4     PC

0        x      x      x      x 0x0000
c   0x0064      x      x      x 0x0001
c   0x0064 0x0002      x      x 0x0002
c   0x0064 0x0002 0x0190      x 0x0003

program(0x0164, 0x0202, 0xE312)
*/

/* Test case MULT:
CLK     R1     R2     R3     R4     PC

0        x      x      x      x  0x0000
c   0x0005      x      x      x  0x0001
c   0x0005 0x0006      x      x  0x0002
c   0x0005 0x0006      x  0x001e 0x0003
c   0x0002 0x0006      x  0x001e 0x0004
c   0x0002 0x00012     x  0x001e 0x0005
c   0x0002 0x00012 0x0024 0x001e 0x0006

program(0x0105, 0x0206, 0xD412, 0x0102, 0x0212, 0xD312)
*/

/* Test case ROR:
CLK     R1     R2     R3     R4     PC

0        x      x      x      x 0x0000
c   0x0064      x      x      x 0x0001
c   0x0064 0x0002      x      x 0x0002
c   0x0064 0x0002 0x0019      x 0x0003

program(0x0164, 0x0202, 0xC312)
*/

/* Test case MOVN:
CLK     R1     R2     R3     R4     PC

0        x      x      x      x 0x0000
c   0x0004      x      x      x 0x0001
c   0x0004 0xfffc      x      x 0x0002
c   0x0005 0xfffc      x      x 0x0003
c   0x0005 0xfffb      x      x 0x0004

program(0x0104, 0x2204, 0x0105, 0x2205)
*/

/* Test case CPU:
# assert these registers can be tested
CLK R1 R2 R3 R4 FL PC

program(0)  # assert program memory exists
init R1=0;  # assert we can initialise R1
init R2=0;  # assert we can initialise R2
init R3=0;  # assert we can initialise R3
init R4=0;  # assert we can initialise R4
init FL=0;  # assert we can initialise FL
init PC=0;  # assert we can initialise PC

0 0 0 0 0 0 0
*/

/* Test case GP_PC:
CLK     R1     R2     R3     R4     PC

init R1=0x5;
init R2=0x98;
0        x      x      x      x 0x0000
c   0x0005 0x0098      x      x 0x0001
c   0x0005 0x0098      x      x 0x0002
c   0x0005 0x0002      x      x 0x0003
c   0x0005 0x0002      x      x 0x0005

program(0x8000,0x8000,0x8260,0x8610,0x03ff,0x0000)
*/

/* Test case MOVL:
CLK     R1     R2     R3     R4     PC

0        x      x      x      x 0x0000
c   0x00ff      x      x      x 0x0001
c   0x0000      x      x      x 0x0002
c   0x0000 0x000c      x      x 0x0003
c   0x0000 0x000c 0x000d      x 0x0004
c   0x0000 0x000c 0x000d 0x00a3 0x0005

program(0x01ff,0x0100,0x020c,0x030d,0x04a3)
*/

/* Test case READ_FLAGS:
CLK     R1     R2     R3     R4     PC

init R1=0x76;
init R4=0xF;
0        x      x      x      x 0x0000
c   0x0076 0x0000      x 0x000f 0x0001
c   0x0076 0x0000      x 0x000f 0x0002
c   0x0076 0x0000 0x0005 0x000f 0x0003

program(0x9211,0x8350,0xa334)
*/

/* Test case SETH:
CLK     R1     R2     R3     R4     PC

init R1=0xAD;
init R2=0x0D;
init R3=0xEF;
init R4=0xAD;
0        x      x      x      x 0x0000
c   0xdead 0x000d 0x00ef 0x00ad 0x0001
c   0xdead 0xf00d 0x00ef 0x00ad 0x0002
c   0xdead 0xf00d 0xbeef 0x00ad 0x0003
c   0xdead 0xf00d 0xbeef 0x0bad 0x0004

program(0x11de,0x12f0,0x13be,0x140b)
*/

/* Test case FLAGS:
CLK     R1     R2     R3     R4   FLAG     PC

declare FLAG = FL & 0xF;

init R1=1;
init R2=0xFFFF;
init R3=0x7FFF;
init R4=0x8000;
0        x      x      x      x      x 0x0000
c   0x0001 0xffff 0x7fff 0x8000 0x0001 0x0001
c   0x0001 0xffff 0x7fff 0x8000 0x0005 0x0002
c   0x0001 0xffff 0x7fff 0x8000 0x0005 0x0003
c   0x0001 0xffff 0x7fff 0x8000 0x0000 0x0004
c   0x0001 0xffff 0x7fff 0x8000 0x0006 0x0005
c   0x0001 0xffff 0x7fff 0x8000 0x0006 0x0006
c   0x0001 0xffff 0x7fff 0x8000 0x0002 0x0007
c   0x0001 0xffff 0x7fff 0x8000 0x0002 0x0008
c   0x0001 0xffff 0x7fff 0x8000 0x000c 0x0009
c   0x0001 0xffff 0x7fff 0x8000 0x0004 0x000a
c   0x0001 0xffff 0x7fff 0x8000 0x000c 0x000b
c   0x0001 0xffff 0x7fff 0x8000 0x000a 0x000c

program(0x8000,0x8012,0x9011,0x9012,0x8022,0x9021,0x8034,0x8041,0x9041,0x9031,0x9043,0x8013)
*/

/* Test case LDR:
CLK     R1     R2     R3     R4     PC

init R1=0x3;
0        x      x      x      x 0x0000
c   0x0003 0x5200      x      x 0x0001
c   0x0003 0x5200 0x9876      x 0x0002

program(0x5200,0x5310,0x0000,0x9876)
*/

/* Test case ALU:
CLK     R1     R2     R3     R4   FLAG     PC

declare FLAG = FL & 0xF;

init R1=0x1A;
init R2=0xF000;
init R2=0xCDFF;
0        x      x      x      x      x 0x0000
c   0x001a 0xcdff      x 0xce19 0x0002 0x0001
c   0x001a 0xcdff      x 0x001a 0x0000 0x0002
c   0x001a 0xcdff      x 0xcdff 0x0006 0x0003
c   0x001a 0xcdff      x 0x3201 0x0000 0x0004
c   0x001a 0xcdff      x 0x0000 0x0001 0x0005
c   0x001a 0xcdff      x 0x0000 0x0001 0x0006
c   0x001a 0xcdff      x 0xcde5 0x0002 0x0007
c   0x001a 0xcdff      x 0xcde5 0x0002 0x0008
c   0x0000 0xcdff      x 0xcde5 0x0001 0x0009
c   0x0000 0x0000      x 0xcde5 0x0001 0x000a

program(0x8412,0xa421,0x9423,0x9432,0xa413,0xa431,0xb412,0xb012,0x8100,0x8230)
*/

/* Test case STR:
CLK     R1     R2     R3     R4     PC

init R1=0x3;
init R2=0xDAF5;
0        x      x      x      x 0x0000
c   0x0003 0xdaf5      x      x 0x0001
c   0x0003 0xdaf5 0xdaf5      x 0x0002

program(0x4210,0x5310,0x0000,0x0000)
*/

/* Test case JUMPS:
CLK     R1     R2     R3     R4     PC

0        x      x      x      x 0x0000
c        x      x      x 0x0003 0x0001
c   0x0001      x      x 0x0003 0x0002
c   0x0001      x      x 0x0003 0x0005
c   0x0001      x 0x0003 0x0003 0x0006
c   0x0001      x 0x0003 0x0003 0x0003
c   0x0001 0x0003 0x0003 0x0003 0x0004
c   0x0001 0x0003 0x0003 0x0003 0x0007
c   0x0001 0x0003 0x0003 0x0009 0x0008
c   0x0001 0x0003 0x0003 0x0009 0x000a

program(0x0403,0x8160,0x8664,0x0203,0x8662,0x0303,0x9663,0x0409,0x8614,0x8660,0x0000)
*/

/* Test case ADD:
CLK     R1     R2     R3     R4     PC

init R1=0x87;
init R2=0x93;
0        x      x      x      x 0x0000
c   0x0087 0x0093 0x011a      x 0x0001
c   0x0087 0x0093 0x011a 0x01ad 0x0002
c   0x010e 0x0093 0x011a 0x01ad 0x0003

program(0x8321,0x8432,0x8111)
*/

/* Test case REC:
CLK     R1     R2     R3     R4     PC

0        x      x      x      x 0x0000
c        x      x      x 0x0000 0x0001
c   0x0020      x      x 0x0000 0x0002
c   0x0020 0x0008      x 0x0000 0x0003
c   0x0020 0x0008 0x0001 0x0000 0x0004
c   0x0021 0x0008 0x0001 0x0000 0x0005
c   0x0021 0x0008 0x0001 0xffff 0x0006
c   0x0021 0x0008 0x001f 0xffff 0x0007
c   0x0021 0x0008 0x001f 0xffff 0x0008
c   0x0021 0x0008 0x001f 0xffff 0x0009
c   0x0021 0x0008 0x001f 0xffff 0x000a
c   0x0021 0x0008 0x0001 0xffff 0x000b
c   0x0021 0x0008 0x0001 0xfffe 0x000c
c   0x0021 0x0008 0x0001 0xfffe 0x000d
c   0x000f 0x0008 0x0001 0xfffe 0x000e
c   0x000f 0x0008 0x0001 0xfffd 0x000f
c   0x000f 0x0008 0x0001 0xfffd 0x0010
c   0x000f 0x0007 0x0001 0xfffd 0x0011
c   0xfffe 0x0007 0x0001 0xfffd 0x0012
c   0x0021 0x0007 0x0001 0xfffd 0x0013
c   0x0022 0x0007 0x0001 0xfffd 0x0014
c   0x0022 0x0007 0x0001 0xfffc 0x0015
c   0x0022 0x0007 0x0018 0xfffc 0x0016
c   0x0022 0x0007 0x0018 0xfffc 0x0017
c   0x0022 0x0007 0x0018 0xfffc 0x0008
c   0x0022 0x0007 0x0018 0xfffc 0x0009
c   0x0022 0x0007 0x0018 0xfffc 0x000a
c   0x0022 0x0007 0x0001 0xfffc 0x000b
c   0x0022 0x0007 0x0001 0xfffb 0x000c
c   0x0022 0x0007 0x0001 0xfffb 0x000d
c   0x0004 0x0007 0x0001 0xfffb 0x000e
c   0x0004 0x0007 0x0001 0xfffa 0x000f
c   0x0004 0x0007 0x0001 0xfffa 0x0010
c   0x0004 0x0006 0x0001 0xfffa 0x0011
c   0xfffb 0x0006 0x0001 0xfffa 0x0012
c   0x0022 0x0006 0x0001 0xfffa 0x0013
c   0x0023 0x0006 0x0001 0xfffa 0x0014
c   0x0023 0x0006 0x0001 0xfff9 0x0015
c   0x0023 0x0006 0x0018 0xfff9 0x0016
c   0x0023 0x0006 0x0018 0xfff9 0x0017
c   0x0023 0x0006 0x0018 0xfff9 0x0008
c   0x0023 0x0006 0x0018 0xfff9 0x0009
c   0x0023 0x0006 0x0018 0xfff9 0x000a
c   0x0023 0x0006 0x0001 0xfff9 0x000b
c   0x0023 0x0006 0x0001 0xfff8 0x000c
c   0x0023 0x0006 0x0001 0xfff8 0x000d
c   0x0005 0x0006 0x0001 0xfff8 0x000e
c   0x0005 0x0006 0x0001 0xfff7 0x000f
c   0x0005 0x0006 0x0001 0xfff7 0x0010
c   0x0005 0x0005 0x0001 0xfff7 0x0011
c   0xfff8 0x0005 0x0001 0xfff7 0x0012
c   0x0023 0x0005 0x0001 0xfff7 0x0013
c   0x0024 0x0005 0x0001 0xfff7 0x0014
c   0x0024 0x0005 0x0001 0xfff6 0x0015
c   0x0024 0x0005 0x0018 0xfff6 0x0016
c   0x0024 0x0005 0x0018 0xfff6 0x0017
c   0x0024 0x0005 0x0018 0xfff6 0x0008
c   0x0024 0x0005 0x0018 0xfff6 0x0009
c   0x0024 0x0005 0x0018 0xfff6 0x000a
c   0x0024 0x0005 0x0001 0xfff6 0x000b
c   0x0024 0x0005 0x0001 0xfff5 0x000c
c   0x0024 0x0005 0x0001 0xfff5 0x000d
c   0x0006 0x0005 0x0001 0xfff5 0x000e
c   0x0006 0x0005 0x0001 0xfff4 0x000f
c   0x0006 0x0005 0x0001 0xfff4 0x0010
c   0x0006 0x0004 0x0001 0xfff4 0x0011
c   0xfff5 0x0004 0x0001 0xfff4 0x0012
c   0x0024 0x0004 0x0001 0xfff4 0x0013
c   0x0025 0x0004 0x0001 0xfff4 0x0014
c   0x0025 0x0004 0x0001 0xfff3 0x0015
c   0x0025 0x0004 0x0018 0xfff3 0x0016
c   0x0025 0x0004 0x0018 0xfff3 0x0017
c   0x0025 0x0004 0x0018 0xfff3 0x0008
c   0x0025 0x0004 0x0018 0xfff3 0x0009
c   0x0025 0x0004 0x0018 0xfff3 0x000a
c   0x0025 0x0004 0x0001 0xfff3 0x000b
c   0x0025 0x0004 0x0001 0xfff2 0x000c
c   0x0025 0x0004 0x0001 0xfff2 0x000d
c   0x0007 0x0004 0x0001 0xfff2 0x000e
c   0x0007 0x0004 0x0001 0xfff1 0x000f
c   0x0007 0x0004 0x0001 0xfff1 0x0010
c   0x0007 0x0003 0x0001 0xfff1 0x0011
c   0xfff2 0x0003 0x0001 0xfff1 0x0012
c   0x0025 0x0003 0x0001 0xfff1 0x0013
c   0x0026 0x0003 0x0001 0xfff1 0x0014
c   0x0026 0x0003 0x0001 0xfff0 0x0015
c   0x0026 0x0003 0x0018 0xfff0 0x0016
c   0x0026 0x0003 0x0018 0xfff0 0x0017
c   0x0026 0x0003 0x0018 0xfff0 0x0008
c   0x0026 0x0003 0x0018 0xfff0 0x0009
c   0x0026 0x0003 0x0018 0xfff0 0x000a
c   0x0026 0x0003 0x0001 0xfff0 0x000b
c   0x0026 0x0003 0x0001 0xffef 0x000c
c   0x0026 0x0003 0x0001 0xffef 0x000d
c   0x0008 0x0003 0x0001 0xffef 0x000e
c   0x0008 0x0003 0x0001 0xffee 0x000f
c   0x0008 0x0003 0x0001 0xffee 0x0010
c   0x0008 0x0002 0x0001 0xffee 0x0011
c   0xffef 0x0002 0x0001 0xffee 0x0012
c   0x0026 0x0002 0x0001 0xffee 0x0013
c   0x0027 0x0002 0x0001 0xffee 0x0014
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*/

/* Test case SUB:
CLK     R1     R2     R3     R4     PC

init R4=0x27;
init R2=0x93;
0        x      x      x      x 0x0000
c   0xff94 0x0093      x 0x0027 0x0001
c   0xff94 0x0093 0x006c 0x0027 0x0002
c   0xff94 0x00d8 0x006c 0x0027 0x0003
c   0xff94 0x00d8 0x006c 0xff28 0x0004

program(0x9142,0x9324,0x9231,0x9413)
*/

/* Test case MEM:
CLK     R1     R2     R3     R4     PC

0        x      x      x      x 0x0000
c   0x000a      x      x      x 0x0001
c   0x000a      x      x      x 0x0002
c   0x000a 0xba55      x      x 0x0003
c   0x000a 0xba55 0xba55      x 0x0004
c   0x000a 0xba55 0xba55 0x0005 0x0005
c   0x000f 0xba55 0xba55 0x0005 0x0006
c   0x000f 0xba5a 0xba55 0x0005 0x0007
c   0x000f 0xba5a 0xba55 0x0005 0x0008
c   0x000f 0xba5a 0xba55 0xba5a 0x0009

program(0x010a,0x9000,0x5210,0x5310,0x0405,0x8114,0x8224,0x4210,0x5410,0x0000,0xba55)
*/

/* Test case AND:
CLK     R1     R2     R3     R4     PC

init R1=0xF0AE;
init R3=0x0FCF;
0        x      x      x      x 0x0000
c   0xf0ae      x 0x0fcf 0x008e 0x0001
c   0xf0ae 0x008e 0x0fcf 0x008e 0x0002
c   0x008e 0x008e 0x0fcf 0x008e 0x0003

program(0xa413,0xa231,0xa124)
*/

/* Test case FIB:
CLK     R1     R2     R3     R4   FLAG     PC

declare FLAG = FL & 0xF;

0        x      x      x      x      x 0x0000
c   0x0001      x      x      x      x 0x0001
c   0x0001 0x0000      x      x      x 0x0002
c   0x0001 0x0000 0x0019      x      x 0x0003
c   0x0001 0x0000 0x0019      x 0x0004 0x0004
c   0x0001 0x0000 0x0019      x 0x0004 0x0005
c   0x0001 0x0000 0x0019 0x0001 0x0000 0x0006
c   0x0000 0x0000 0x0019 0x0001 0x0001 0x0007
c   0x0000 0x0001 0x0019 0x0001 0x0000 0x0008
c   0x0000 0x0001 0x0019 0x0001 0x0000 0x0009
c   0x0000 0x0001 0x0018 0x0001 0x0004 0x000a
c   0x0000 0x0001 0x0018 0x0001 0x0004 0x0003
c   0x0000 0x0001 0x0018 0x0001 0x0004 0x0004
c   0x0000 0x0001 0x0018 0x0001 0x0004 0x0005
c   0x0000 0x0001 0x0018 0x0001 0x0000 0x0006
c   0x0001 0x0001 0x0018 0x0001 0x0000 0x0007
c   0x0001 0x0001 0x0018 0x0001 0x0000 0x0008
c   0x0001 0x0001 0x0018 0x0001 0x0000 0x0009
c   0x0001 0x0001 0x0017 0x0001 0x0004 0x000a
c   0x0001 0x0001 0x0017 0x0001 0x0004 0x0003
c   0x0001 0x0001 0x0017 0x0001 0x0004 0x0004
c   0x0001 0x0001 0x0017 0x0001 0x0004 0x0005
c   0x0001 0x0001 0x0017 0x0002 0x0000 0x0006
c   0x0001 0x0001 0x0017 0x0002 0x0000 0x0007
c   0x0001 0x0002 0x0017 0x0002 0x0000 0x0008
c   0x0001 0x0002 0x0017 0x0001 0x0000 0x0009
c   0x0001 0x0002 0x0016 0x0001 0x0004 0x000a
c   0x0001 0x0002 0x0016 0x0001 0x0004 0x0003
c   0x0001 0x0002 0x0016 0x0001 0x0004 0x0004
c   0x0001 0x0002 0x0016 0x0001 0x0004 0x0005
c   0x0001 0x0002 0x0016 0x0003 0x0000 0x0006
c   0x0002 0x0002 0x0016 0x0003 0x0000 0x0007
c   0x0002 0x0003 0x0016 0x0003 0x0000 0x0008
c   0x0002 0x0003 0x0016 0x0001 0x0000 0x0009
c   0x0002 0x0003 0x0015 0x0001 0x0004 0x000a
c   0x0002 0x0003 0x0015 0x0001 0x0004 0x0003
c   0x0002 0x0003 0x0015 0x0001 0x0004 0x0004
c   0x0002 0x0003 0x0015 0x0001 0x0004 0x0005
c   0x0002 0x0003 0x0015 0x0005 0x0000 0x0006
c   0x0003 0x0003 0x0015 0x0005 0x0000 0x0007
c   0x0003 0x0005 0x0015 0x0005 0x0000 0x0008
c   0x0003 0x0005 0x0015 0x0001 0x0000 0x0009
c   0x0003 0x0005 0x0014 0x0001 0x0004 0x000a
c   0x0003 0x0005 0x0014 0x0001 0x0004 0x0003
c   0x0003 0x0005 0x0014 0x0001 0x0004 0x0004
c   0x0003 0x0005 0x0014 0x0001 0x0004 0x0005
c   0x0003 0x0005 0x0014 0x0008 0x0000 0x0006
c   0x0005 0x0005 0x0014 0x0008 0x0000 0x0007
c   0x0005 0x0008 0x0014 0x0008 0x0000 0x0008
c   0x0005 0x0008 0x0014 0x0001 0x0000 0x0009
c   0x0005 0x0008 0x0013 0x0001 0x0004 0x000a
c   0x0005 0x0008 0x0013 0x0001 0x0004 0x0003
c   0x0005 0x0008 0x0013 0x0001 0x0004 0x0004
c   0x0005 0x0008 0x0013 0x0001 0x0004 0x0005
c   0x0005 0x0008 0x0013 0x000d 0x0000 0x0006
c   0x0008 0x0008 0x0013 0x000d 0x0000 0x0007
c   0x0008 0x000d 0x0013 0x000d 0x0000 0x0008
c   0x0008 0x000d 0x0013 0x0001 0x0000 0x0009
c   0x0008 0x000d 0x0012 0x0001 0x0004 0x000a
c   0x0008 0x000d 0x0012 0x0001 0x0004 0x0003
c   0x0008 0x000d 0x0012 0x0001 0x0004 0x0004
c   0x0008 0x000d 0x0012 0x0001 0x0004 0x0005
c   0x0008 0x000d 0x0012 0x0015 0x0000 0x0006
c   0x000d 0x000d 0x0012 0x0015 0x0000 0x0007
c   0x000d 0x0015 0x0012 0x0015 0x0000 0x0008
c   0x000d 0x0015 0x0012 0x0001 0x0000 0x0009
c   0x000d 0x0015 0x0011 0x0001 0x0004 0x000a
c   0x000d 0x0015 0x0011 0x0001 0x0004 0x0003
c   0x000d 0x0015 0x0011 0x0001 0x0004 0x0004
c   0x000d 0x0015 0x0011 0x0001 0x0004 0x0005
c   0x000d 0x0015 0x0011 0x0022 0x0000 0x0006
c   0x0015 0x0015 0x0011 0x0022 0x0000 0x0007
c   0x0015 0x0022 0x0011 0x0022 0x0000 0x0008
c   0x0015 0x0022 0x0011 0x0001 0x0000 0x0009
c   0x0015 0x0022 0x0010 0x0001 0x0004 0x000a
c   0x0015 0x0022 0x0010 0x0001 0x0004 0x0003
c   0x0015 0x0022 0x0010 0x0001 0x0004 0x0004
c   0x0015 0x0022 0x0010 0x0001 0x0004 0x0005
c   0x0015 0x0022 0x0010 0x0037 0x0000 0x0006
c   0x0022 0x0022 0x0010 0x0037 0x0000 0x0007
c   0x0022 0x0037 0x0010 0x0037 0x0000 0x0008
c   0x0022 0x0037 0x0010 0x0001 0x0000 0x0009
c   0x0022 0x0037 0x000f 0x0001 0x0004 0x000a
c   0x0022 0x0037 0x000f 0x0001 0x0004 0x0003
c   0x0022 0x0037 0x000f 0x0001 0x0004 0x0004
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*/

/* Test case XOR:
CLK     R1     R2     R3     R4     PC

init R4=0xF0AE;
init R3=0x0FC8;
0        x      x      x      x 0x0000
c   0xff66      x 0x0fc8 0xf0ae 0x0001
c   0xff66 0xff66 0x0fc8 0xf0ae 0x0002

program(0xb143,0xb234)
*/

/* Test case COND:
CLK     R1     R2     R3     R4     PC     FL
0        x      x      x      x 0x0000      x
c   0x0000      x      x      x 0x0001      x
c   0x0000 0x0000      x      x 0x0002      x
c   0x0000 0x0000 0x0016      x 0x0003      x
c   0x0000 0x0000 0x0016 0x0001 0x0004      x
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*/
