// Digital circuit flag_setters_basic.dig as structural Verilog
module flag_setters_basic (
  input  [15:0] RES,
  input  [15:0] A,
  input  [15:0] B,
  input  [1:0] op,
  input  [15:0] IN,
  input  Carry_add,
  input  Carry_sub,
  output Z,
  output N,
  output C,
  output V
);

  wire and_3_out, not_1_out, not_2_out, xnor_1_out, xor_1_out, Z_flag_eq;

  not not_1 (not_1_out, op[1]);
  and and_1 (N, IN[15], 1'b1);
  Comparator #(.Bits(16)) Z_flag (.a(IN), .b({16{1'b0}}), .eq(Z_flag_eq));  // open: gt, lt
  xor xor_1 (xor_1_out, RES[15], A[15]);
  xnor xnor_1 (xnor_1_out, A[15], B[15], op[0]);
  and and_2 (Z, 1'b1, Z_flag_eq);
  and and_3 (and_3_out, xor_1_out, xnor_1_out, not_1_out);
  Multiplexer #(.Selector_Bits(2)) multiplexer_1 (
    .sel(op), .in_0(and_3_out), .in_1(and_3_out), .in_2(1'b0), .in_3(1'b0), .out(V));
  not not_2 (not_2_out, Carry_sub);
  Multiplexer #(.Selector_Bits(2)) multiplexer_2 (
    .sel(op), .in_0(Carry_add), .in_1(not_2_out), .in_2(1'b0), .in_3(1'b0), .out(C));
endmodule
