// Digital circuit flags_setter.dig as structural Verilog
module flags_setter (
  input  [15:0] RES,
  input  [15:0] A,
  input  [15:0] B,
  input  [2:0] op,
  input  [15:0] IN,
  input  Carry_add,
  input  Carry_sub,
  input  Mul_V,
  input  [15:0] R,
  input  Div_V,
  output Z,
  output N,
  output C,
  output V,
  output [15:0] REM
);

  wire and_3_out, not_1_out, xnor_1_out, xor_1_out, Z_flag_eq;

  Comparator #(.Bits(16)) Z_flag (.a(IN), .b({16{1'b0}}), .eq(Z_flag_eq));  // open: gt, lt
  not not_1 (not_1_out, op[1]);
  and and_1 (N, IN[15], 1'b1);
  xor xor_1 (xor_1_out, RES[15], A[15]);
  xnor xnor_1 (xnor_1_out, A[15], B[15], op[0]);
  and and_2 (Z, 1'b1, Z_flag_eq);
  and and_3 (and_3_out, xor_1_out, xnor_1_out, not_1_out);
  Multiplexer #(.Selector_Bits(3)) multiplexer_1 (
    .sel(op), .in_0(and_3_out), .in_1(and_3_out), .in_2(1'b0), .in_3(1'b0), .in_4(1'b0), .in_5(Mul_V),
    .in_6(1'b0), .in_7(Div_V), .out(V));
  Multiplexer #(.Selector_Bits(3)) multiplexer_2 (
    .sel(op), .in_0(Carry_add), .in_1(Carry_sub), .in_2(1'b0), .in_3(1'b0), .in_4(1'b0), .in_5(1'b0),
    .in_6(1'b0), .in_7(1'b0), .out(C));

  assign REM = R;

  // Notes on the sheet:
  //   R: Remainder from division
  //   REM: Remainder from division
endmodule
