// Digital circuit logical_shift.dig as structural Verilog
module logical_shift (
  input  [15:0] A,
  input  [3:0] shift,
  output [15:0] OUT
);

  Multiplexer #(.Selector_Bits(4)) multiplexer_1 (
    .sel(shift), .in_0(A[15]), .in_1(A[14]), .in_2(A[13]), .in_3(A[12]), .in_4(A[11]), .in_5(A[10]),
    .in_6(A[9]), .in_7(A[8]), .in_8(A[7]), .in_9(A[6]), .in_10(A[5]), .in_11(A[4]), .in_12(A[3]),
    .in_13(A[2]), .in_14(A[1]), .in_15(A[0]), .out(OUT[15]));
  Multiplexer #(.Selector_Bits(4)) multiplexer_2 (
    .sel(shift), .in_0(A[14]), .in_1(A[13]), .in_2(A[12]), .in_3(A[11]), .in_4(A[10]), .in_5(A[9]),
    .in_6(A[8]), .in_7(A[7]), .in_8(A[6]), .in_9(A[5]), .in_10(A[4]), .in_11(A[3]), .in_12(A[2]),
    .in_13(A[1]), .in_14(A[0]), .in_15(1'b0), .out(OUT[14]));
  Multiplexer #(.Selector_Bits(4)) multiplexer_3 (
    .sel(shift), .in_0(A[13]), .in_1(A[12]), .in_2(A[11]), .in_3(A[10]), .in_4(A[9]), .in_5(A[8]),
    .in_6(A[7]), .in_7(A[6]), .in_8(A[5]), .in_9(A[4]), .in_10(A[3]), .in_11(A[2]), .in_12(A[1]),
    .in_13(A[0]), .in_14(1'b0), .in_15(1'b0), .out(OUT[13]));
  Multiplexer #(.Selector_Bits(4)) multiplexer_4 (
    .sel(shift), .in_0(A[12]), .in_1(A[11]), .in_2(A[10]), .in_3(A[9]), .in_4(A[8]), .in_5(A[7]),
    .in_6(A[6]), .in_7(A[5]), .in_8(A[4]), .in_9(A[3]), .in_10(A[2]), .in_11(A[1]), .in_12(A[0]),
    .in_13(1'b0), .in_14(1'b0), .in_15(1'b0), .out(OUT[12]));
  Multiplexer #(.Selector_Bits(4)) multiplexer_5 (
    .sel(shift), .in_0(A[11]), .in_1(A[10]), .in_2(A[9]), .in_3(A[8]), .in_4(A[7]), .in_5(A[6]), .in_6(A[5]),
    .in_7(A[4]), .in_8(A[3]), .in_9(A[2]), .in_10(A[1]), .in_11(A[0]), .in_12(1'b0), .in_13(1'b0),
    .in_14(1'b0), .in_15(1'b0), .out(OUT[11]));
  Multiplexer #(.Selector_Bits(4)) multiplexer_6 (
    .sel(shift), .in_0(A[10]), .in_1(A[9]), .in_2(A[8]), .in_3(A[7]), .in_4(A[6]), .in_5(A[5]), .in_6(A[4]),
    .in_7(A[3]), .in_8(A[2]), .in_9(A[1]), .in_10(A[0]), .in_11(1'b0), .in_12(1'b0), .in_13(1'b0),
    .in_14(1'b0), .in_15(1'b0), .out(OUT[10]));
  Multiplexer #(.Selector_Bits(4)) multiplexer_7 (
    .sel(shift), .in_0(A[9]), .in_1(A[8]), .in_2(A[7]), .in_3(A[6]), .in_4(A[5]), .in_5(A[4]), .in_6(A[3]),
    .in_7(A[2]), .in_8(A[1]), .in_9(A[0]), .in_10(1'b0), .in_11(1'b0), .in_12(1'b0), .in_13(1'b0),
    .in_14(1'b0), .in_15(1'b0), .out(OUT[9]));
  Multiplexer #(.Selector_Bits(4)) multiplexer_8 (
    .sel(shift), .in_0(A[8]), .in_1(A[7]), .in_2(A[6]), .in_3(A[5]), .in_4(A[4]), .in_5(A[3]), .in_6(A[2]),
    .in_7(A[1]), .in_8(A[0]), .in_9(1'b0), .in_10(1'b0), .in_11(1'b0), .in_12(1'b0), .in_13(1'b0),
    .in_14(1'b0), .in_15(1'b0), .out(OUT[8]));
  Multiplexer #(.Selector_Bits(4)) multiplexer_9 (
    .sel(shift), .in_0(A[7]), .in_1(A[6]), .in_2(A[5]), .in_3(A[4]), .in_4(A[3]), .in_5(A[2]), .in_6(A[1]),
    .in_7(A[0]), .in_8(1'b0), .in_9(1'b0), .in_10(1'b0), .in_11(1'b0), .in_12(1'b0), .in_13(1'b0),
    .in_14(1'b0), .in_15(1'b0), .out(OUT[7]));
  Multiplexer #(.Selector_Bits(4)) multiplexer_10 (
    .sel(shift), .in_0(A[6]), .in_1(A[5]), .in_2(A[4]), .in_3(A[3]), .in_4(A[2]), .in_5(A[1]), .in_6(A[0]),
    .in_7(1'b0), .in_8(1'b0), .in_9(1'b0), .in_10(1'b0), .in_11(1'b0), .in_12(1'b0), .in_13(1'b0),
    .in_14(1'b0), .in_15(1'b0), .out(OUT[6]));
  Multiplexer #(.Selector_Bits(4)) multiplexer_11 (
    .sel(shift), .in_0(A[5]), .in_1(A[4]), .in_2(A[3]), .in_3(A[2]), .in_4(A[1]), .in_5(A[0]), .in_6(1'b0),
    .in_7(1'b0), .in_8(1'b0), .in_9(1'b0), .in_10(1'b0), .in_11(1'b0), .in_12(1'b0), .in_13(1'b0),
    .in_14(1'b0), .in_15(1'b0), .out(OUT[5]));
  Multiplexer #(.Selector_Bits(4)) multiplexer_12 (
    .sel(shift), .in_0(A[4]), .in_1(A[3]), .in_2(A[2]), .in_3(A[1]), .in_4(A[0]), .in_5(1'b0), .in_6(1'b0),
    .in_7(1'b0), .in_8(1'b0), .in_9(1'b0), .in_10(1'b0), .in_11(1'b0), .in_12(1'b0), .in_13(1'b0),
    .in_14(1'b0), .in_15(1'b0), .out(OUT[4]));
  Multiplexer #(.Selector_Bits(4)) multiplexer_13 (
    .sel(shift), .in_0(A[3]), .in_1(A[2]), .in_2(A[1]), .in_3(A[0]), .in_4(1'b0), .in_5(1'b0), .in_6(1'b0),
    .in_7(1'b0), .in_8(1'b0), .in_9(1'b0), .in_10(1'b0), .in_11(1'b0), .in_12(1'b0), .in_13(1'b0),
    .in_14(1'b0), .in_15(1'b0), .out(OUT[3]));
  Multiplexer #(.Selector_Bits(4)) multiplexer_14 (
    .sel(shift), .in_0(A[2]), .in_1(A[1]), .in_2(A[0]), .in_3(1'b0), .in_4(1'b0), .in_5(1'b0), .in_6(1'b0),
    .in_7(1'b0), .in_8(1'b0), .in_9(1'b0), .in_10(1'b0), .in_11(1'b0), .in_12(1'b0), .in_13(1'b0),
    .in_14(1'b0), .in_15(1'b0), .out(OUT[2]));
  Multiplexer #(.Selector_Bits(4)) multiplexer_15 (
    .sel(shift), .in_0(A[1]), .in_1(A[0]), .in_2(1'b0), .in_3(1'b0), .in_4(1'b0), .in_5(1'b0), .in_6(1'b0),
    .in_7(1'b0), .in_8(1'b0), .in_9(1'b0), .in_10(1'b0), .in_11(1'b0), .in_12(1'b0), .in_13(1'b0),
    .in_14(1'b0), .in_15(1'b0), .out(OUT[1]));
  Multiplexer #(.Selector_Bits(4)) multiplexer_16 (
    .sel(shift), .in_0(A[0]), .in_1(1'b0), .in_2(1'b0), .in_3(1'b0), .in_4(1'b0), .in_5(1'b0), .in_6(1'b0),
    .in_7(1'b0), .in_8(1'b0), .in_9(1'b0), .in_10(1'b0), .in_11(1'b0), .in_12(1'b0), .in_13(1'b0),
    .in_14(1'b0), .in_15(1'b0), .out(OUT[0]));

  // Notes on the sheet:
  //   15
  //   14
  //   13
  //   12
  //   11
  //   10
  //   9
  //   8
  //   7
  //   6
  //   5
  //   4
  //   3
  //   2
  //   1
  //   0
endmodule

/* Test case Left Shift:
A shift OUT
loop(i,100)
	let y = random(1<<16);
        let shift = random(1<<4);
	(y) (shift) (y<<shift)
end loop
*/
