// Digital circuit main_decoder.dig as structural Verilog
module main_decoder (
  input  [3:0] opcode,
  input  EXEC,
  input  CLK,
  output [2:0] ALUOP,
  output STR,
  output WE,
  output LDR,
  output FLEN,
  output DIV,
  output STRR,
  output LDRR,
  output SHADOW_en
);

  wire and_2_out, and_5_out, decoder_1_out_3, decoder_1_out_4, decoder_1_out_5, decoder_1_out_6,
       decoder_1_out_7, decoder_1_out_8, decoder_1_out_9, decoder_1_out_10, decoder_1_out_11,
       decoder_1_out_12, decoder_1_out_13, decoder_1_out_14, not_1_out, or_2_out, STR_t;
  wire [0:0] not_2_out;

  Decoder #(.Selector_Bits(4)) decoder_1 (
    .sel(opcode), .out_3(decoder_1_out_3), .out_4(decoder_1_out_4), .out_5(decoder_1_out_5),
    .out_6(decoder_1_out_6), .out_7(decoder_1_out_7), .out_8(decoder_1_out_8), .out_9(decoder_1_out_9),
    .out_10(decoder_1_out_10), .out_11(decoder_1_out_11), .out_12(decoder_1_out_12),
    .out_13(decoder_1_out_13), .out_14(decoder_1_out_14), .out_15(DIV));  // open: out_0, out_1, out_2
  JK_FF jk_ff_1 (.J(decoder_1_out_3), .C(CLK), .K(decoder_1_out_3), .Q(SHADOW_en));  // open: nQ
  or or_1 (FLEN, decoder_1_out_8, decoder_1_out_9, decoder_1_out_10, decoder_1_out_11, decoder_1_out_12, decoder_1_out_13, decoder_1_out_14, DIV);
  and and_1 (STR_t, EXEC, decoder_1_out_4);
  and and_2 (and_2_out, decoder_1_out_5, EXEC);
  not not_1 (not_1_out, decoder_1_out_4);
  and and_3 (STRR, EXEC, decoder_1_out_6);
  and and_4 (LDRR, decoder_1_out_7, EXEC);
  or or_2 (or_2_out, STRR, LDRR);
  not not_2 (not_2_out[0], or_2_out);
  or or_3 (STR, STR_t, STRR);
  or or_4 (LDR, and_2_out, LDRR);
  and and_5 (and_5_out, not_1_out, EXEC);
  Multiplexer #(.Bits(3)) multiplexer_1 (.sel(or_2_out), .in_0(opcode[2:0]), .in_1({2'b00, not_2_out[0]}), .out(ALUOP));
  Multiplexer multiplexer_2 (.sel(STRR), .in_0(and_5_out), .in_1(1'b1), .out(WE));
endmodule
