// Digital circuit main_decoder_basic.dig as structural Verilog
module main_decoder_basic (
  input  [3:0] opcode,
  input  EXEC,
  output [1:0] ALUOP,
  output STR,
  output WE,
  output LDR,
  output FLEN
);

  wire decoder_1_out_4, decoder_1_out_5, decoder_1_out_8, decoder_1_out_9, decoder_1_out_10,
       decoder_1_out_11, decoder_1_out_12, decoder_1_out_13, decoder_1_out_14, not_1_out;

  Decoder #(.Selector_Bits(4)) decoder_1 (
    .sel(opcode), .out_4(decoder_1_out_4), .out_5(decoder_1_out_5), .out_8(decoder_1_out_8),
    .out_9(decoder_1_out_9), .out_10(decoder_1_out_10), .out_11(decoder_1_out_11), .out_12(decoder_1_out_12),
    .out_13(decoder_1_out_13), .out_14(decoder_1_out_14));  // open: out_0, out_1, out_2, out_3, out_6, out_7, out_15
  or or_1 (FLEN, decoder_1_out_8, decoder_1_out_9, decoder_1_out_10, decoder_1_out_11, decoder_1_out_12, decoder_1_out_13, decoder_1_out_14);
  not not_1 (not_1_out, decoder_1_out_4);
  and and_1 (STR, EXEC, decoder_1_out_4);
  and and_2 (LDR, decoder_1_out_5, EXEC);
  and and_3 (WE, not_1_out, EXEC);

  assign ALUOP = opcode[1:0];
endmodule
