// Digital circuit multiply.dig as structural Verilog
module multiply (
  input  [15:0] A,
  input  [15:0] B,
  output [31:0] P,
  output V
);

  wire _32_bit_cla_1_c_out, _32_bit_cla_2_c_out, _32_bit_cla_3_c_out, _32_bit_cla_4_c_out,
       _32_bit_cla_5_c_out, _32_bit_cla_6_c_out, _32_bit_cla_7_c_out, _32_bit_cla_8_c_out,
       _32_bit_cla_9_c_out, _32_bit_cla_10_c_out, _32_bit_cla_11_c_out, or_1_out, or_2_out, or_3_out;
  wire [7:0] _4_bit_multiplier_1_prod, _4_bit_multiplier_2_prod, _4_bit_multiplier_3_prod,
       _4_bit_multiplier_4_prod, _4_bit_multiplier_5_prod, _4_bit_multiplier_6_prod,
       _4_bit_multiplier_7_prod, _4_bit_multiplier_8_prod, _4_bit_multiplier_9_prod,
       _4_bit_multiplier_10_prod, _4_bit_multiplier_11_prod, _4_bit_multiplier_12_prod,
       _4_bit_multiplier_13_prod, _4_bit_multiplier_14_prod, _4_bit_multiplier_15_prod,
       _4_bit_multiplier_16_prod;
  wire [31:0] _8_32_extender_1_out, _8_32_extender_2_out, _8_32_extender_3_out, _8_32_extender_4_out,
       _8_32_extender_5_out, _8_32_extender_6_out, _8_32_extender_7_out, _8_32_extender_8_out,
       _8_32_extender_9_out, _8_32_extender_10_out, _8_32_extender_11_out, _8_32_extender_12_out,
       _8_32_extender_13_out, _8_32_extender_14_out, _8_32_extender_15_out, _8_32_extender_16_out,
       _32_bit_cla_1_s, _32_bit_cla_2_s, _32_bit_cla_3_s, _32_bit_cla_4_s, _32_bit_cla_5_s, _32_bit_cla_6_s,
       _32_bit_cla_7_s, _32_bit_cla_8_s, _32_bit_cla_9_s, _32_bit_cla_10_s, _32_bit_cla_11_s,
       _32_bit_cla_12_s, add_1_s, add_2_s, barrelshifter_1_out, barrelshifter_2_out, barrelshifter_3_out,
       barrelshifter_4_out, barrelshifter_5_out, barrelshifter_6_out, barrelshifter_7_out,
       barrelshifter_8_out, barrelshifter_9_out, barrelshifter_10_out, barrelshifter_11_out,
       barrelshifter_12_out, barrelshifter_13_out, barrelshifter_14_out, barrelshifter_15_out;

  _4_bit_multiplier _4_bit_multiplier_1 (.B(B[3:0]), .A(A[3:0]), .Prod(_4_bit_multiplier_1_prod));
  _8_32_extender _8_32_extender_1 (.IN(_4_bit_multiplier_1_prod), .OUT(_8_32_extender_1_out));
  _4_bit_multiplier _4_bit_multiplier_2 (.B(B[3:0]), .A(A[7:4]), .Prod(_4_bit_multiplier_2_prod));
  _8_32_extender _8_32_extender_2 (.IN(_4_bit_multiplier_2_prod), .OUT(_8_32_extender_2_out));
  _4_bit_multiplier _4_bit_multiplier_3 (.B(B[3:0]), .A(A[11:8]), .Prod(_4_bit_multiplier_3_prod));
  _8_32_extender _8_32_extender_3 (.IN(_4_bit_multiplier_3_prod), .OUT(_8_32_extender_3_out));
  _4_bit_multiplier _4_bit_multiplier_4 (.B(B[3:0]), .A(A[15:12]), .Prod(_4_bit_multiplier_4_prod));
  _8_32_extender _8_32_extender_4 (.IN(_4_bit_multiplier_4_prod), .OUT(_8_32_extender_4_out));
  _4_bit_multiplier _4_bit_multiplier_5 (.B(B[7:4]), .A(A[3:0]), .Prod(_4_bit_multiplier_5_prod));
  _8_32_extender _8_32_extender_5 (.IN(_4_bit_multiplier_5_prod), .OUT(_8_32_extender_5_out));
  _4_bit_multiplier _4_bit_multiplier_6 (.B(B[7:4]), .A(A[7:4]), .Prod(_4_bit_multiplier_6_prod));
  _8_32_extender _8_32_extender_6 (.IN(_4_bit_multiplier_6_prod), .OUT(_8_32_extender_6_out));
  _4_bit_multiplier _4_bit_multiplier_7 (.B(B[7:4]), .A(A[11:8]), .Prod(_4_bit_multiplier_7_prod));
  _8_32_extender _8_32_extender_7 (.IN(_4_bit_multiplier_7_prod), .OUT(_8_32_extender_7_out));
  _4_bit_multiplier _4_bit_multiplier_8 (.B(B[7:4]), .A(A[15:12]), .Prod(_4_bit_multiplier_8_prod));
  _8_32_extender _8_32_extender_8 (.IN(_4_bit_multiplier_8_prod), .OUT(_8_32_extender_8_out));
  _4_bit_multiplier _4_bit_multiplier_9 (.B(B[11:8]), .A(A[3:0]), .Prod(_4_bit_multiplier_9_prod));
  _8_32_extender _8_32_extender_9 (.IN(_4_bit_multiplier_9_prod), .OUT(_8_32_extender_9_out));
  _4_bit_multiplier _4_bit_multiplier_10 (.B(B[11:8]), .A(A[7:4]), .Prod(_4_bit_multiplier_10_prod));
  _8_32_extender _8_32_extender_10 (.IN(_4_bit_multiplier_10_prod), .OUT(_8_32_extender_10_out));
  _4_bit_multiplier _4_bit_multiplier_11 (.B(B[11:8]), .A(A[11:8]), .Prod(_4_bit_multiplier_11_prod));
  _8_32_extender _8_32_extender_11 (.IN(_4_bit_multiplier_11_prod), .OUT(_8_32_extender_11_out));
  _4_bit_multiplier _4_bit_multiplier_12 (.B(B[11:8]), .A(A[15:12]), .Prod(_4_bit_multiplier_12_prod));
  _8_32_extender _8_32_extender_12 (.IN(_4_bit_multiplier_12_prod), .OUT(_8_32_extender_12_out));
  _4_bit_multiplier _4_bit_multiplier_13 (.B(B[15:12]), .A(A[3:0]), .Prod(_4_bit_multiplier_13_prod));
  _8_32_extender _8_32_extender_13 (.IN(_4_bit_multiplier_13_prod), .OUT(_8_32_extender_13_out));
  _4_bit_multiplier _4_bit_multiplier_14 (.B(B[15:12]), .A(A[7:4]), .Prod(_4_bit_multiplier_14_prod));
  _8_32_extender _8_32_extender_14 (.IN(_4_bit_multiplier_14_prod), .OUT(_8_32_extender_14_out));
  _4_bit_multiplier _4_bit_multiplier_15 (.B(B[15:12]), .A(A[11:8]), .Prod(_4_bit_multiplier_15_prod));
  _8_32_extender _8_32_extender_15 (.IN(_4_bit_multiplier_15_prod), .OUT(_8_32_extender_15_out));
  _4_bit_multiplier _4_bit_multiplier_16 (.B(B[15:12]), .A(A[15:12]), .Prod(_4_bit_multiplier_16_prod));
  _8_32_extender _8_32_extender_16 (.IN(_4_bit_multiplier_16_prod), .OUT(_8_32_extender_16_out));
  BarrelShifter #(.Bits(32), .barrelSigned("true")) barrelshifter_1 (
    .in(_8_32_extender_5_out), .shift(7'b0000100), .out(barrelshifter_1_out));
  BarrelShifter #(.Bits(32), .barrelSigned("true")) barrelshifter_2 (
    .in(_8_32_extender_6_out), .shift(7'b0000100), .out(barrelshifter_2_out));
  BarrelShifter #(.Bits(32), .barrelSigned("true")) barrelshifter_3 (
    .in(_8_32_extender_7_out), .shift(7'b0000100), .out(barrelshifter_3_out));
  BarrelShifter #(.Bits(32), .barrelSigned("true")) barrelshifter_4 (
    .in(_8_32_extender_8_out), .shift(7'b0000100), .out(barrelshifter_4_out));
  _32_bit_CLA _32_bit_cla_1 (
    .A(_8_32_extender_1_out), .B(barrelshifter_1_out), .C_in(1'b0), .S(_32_bit_cla_1_s),
    .C_out(_32_bit_cla_1_c_out));
  _32_bit_CLA _32_bit_cla_2 (
    .A(_8_32_extender_2_out), .B(barrelshifter_2_out), .C_in(1'b0), .S(_32_bit_cla_2_s),
    .C_out(_32_bit_cla_2_c_out));
  _32_bit_CLA _32_bit_cla_3 (
    .A(_8_32_extender_3_out), .B(barrelshifter_3_out), .C_in(1'b0), .S(_32_bit_cla_3_s),
    .C_out(_32_bit_cla_3_c_out));
  _32_bit_CLA _32_bit_cla_4 (
    .A(_8_32_extender_4_out), .B(barrelshifter_4_out), .C_in(1'b0), .S(_32_bit_cla_4_s),
    .C_out(_32_bit_cla_4_c_out));
  BarrelShifter #(.Bits(32), .barrelSigned("true")) barrelshifter_5 (
    .in(_8_32_extender_9_out), .shift(7'b0001000), .out(barrelshifter_5_out));
  BarrelShifter #(.Bits(32), .barrelSigned("true")) barrelshifter_6 (
    .in(_8_32_extender_10_out), .shift(7'b0001000), .out(barrelshifter_6_out));
  BarrelShifter #(.Bits(32), .barrelSigned("true")) barrelshifter_7 (
    .in(_8_32_extender_11_out), .shift(7'b0001000), .out(barrelshifter_7_out));
  BarrelShifter #(.Bits(32), .barrelSigned("true")) barrelshifter_8 (
    .in(_8_32_extender_12_out), .shift(7'b0001000), .out(barrelshifter_8_out));
  BarrelShifter #(.Bits(32), .barrelSigned("true")) barrelshifter_9 (
    .in(_8_32_extender_13_out), .shift(7'b0001100), .out(barrelshifter_9_out));
  _32_bit_CLA _32_bit_cla_5 (
    .A(barrelshifter_5_out), .B(_32_bit_cla_1_s), .C_in(_32_bit_cla_1_c_out), .S(_32_bit_cla_5_s),
    .C_out(_32_bit_cla_5_c_out));
  BarrelShifter #(.Bits(32), .barrelSigned("true")) barrelshifter_10 (
    .in(_8_32_extender_14_out), .shift(7'b0001100), .out(barrelshifter_10_out));
  _32_bit_CLA _32_bit_cla_6 (
    .A(barrelshifter_6_out), .B(_32_bit_cla_2_s), .C_in(_32_bit_cla_2_c_out), .S(_32_bit_cla_6_s),
    .C_out(_32_bit_cla_6_c_out));
  BarrelShifter #(.Bits(32), .barrelSigned("true")) barrelshifter_11 (
    .in(_8_32_extender_15_out), .shift(7'b0001100), .out(barrelshifter_11_out));
  _32_bit_CLA _32_bit_cla_7 (
    .A(barrelshifter_7_out), .B(_32_bit_cla_3_s), .C_in(_32_bit_cla_3_c_out), .S(_32_bit_cla_7_s),
    .C_out(_32_bit_cla_7_c_out));
  BarrelShifter #(.Bits(32), .barrelSigned("true")) barrelshifter_12 (
    .in(_8_32_extender_16_out), .shift(7'b0001100), .out(barrelshifter_12_out));
  _32_bit_CLA _32_bit_cla_8 (
    .A(barrelshifter_8_out), .B(_32_bit_cla_4_s), .C_in(_32_bit_cla_4_c_out), .S(_32_bit_cla_8_s),
    .C_out(_32_bit_cla_8_c_out));
  or or_1 (or_1_out, P[16], P[17], P[18], P[19], P[20]);
  or or_2 (or_2_out, P[21], P[22], P[23], P[24], P[25]);
  or or_3 (or_3_out, P[26], P[27], P[28], P[29], P[30]);
  _32_bit_CLA _32_bit_cla_9 (
    .A(barrelshifter_9_out), .B(_32_bit_cla_5_s), .C_in(_32_bit_cla_5_c_out), .S(_32_bit_cla_9_s),
    .C_out(_32_bit_cla_9_c_out));
  _32_bit_CLA _32_bit_cla_10 (
    .A(barrelshifter_10_out), .B(_32_bit_cla_6_s), .C_in(_32_bit_cla_6_c_out), .S(_32_bit_cla_10_s),
    .C_out(_32_bit_cla_10_c_out));
  _32_bit_CLA _32_bit_cla_11 (
    .A(barrelshifter_11_out), .B(_32_bit_cla_7_s), .C_in(_32_bit_cla_7_c_out), .S(_32_bit_cla_11_s),
    .C_out(_32_bit_cla_11_c_out));
  _32_bit_CLA _32_bit_cla_12 (
    .A(barrelshifter_12_out), .B(_32_bit_cla_8_s), .C_in(_32_bit_cla_8_c_out), .S(_32_bit_cla_12_s));  // open: C_out
  or or_4 (V, or_1_out, or_2_out, or_3_out, P[31]);
  BarrelShifter #(.Bits(32), .barrelSigned("true")) barrelshifter_13 (
    .in(_32_bit_cla_10_s), .shift(7'b0000100), .out(barrelshifter_13_out));
  BarrelShifter #(.Bits(32), .barrelSigned("true")) barrelshifter_14 (
    .in(_32_bit_cla_11_s), .shift(7'b0001000), .out(barrelshifter_14_out));
  BarrelShifter #(.Bits(32), .barrelSigned("true")) barrelshifter_15 (
    .in(_32_bit_cla_12_s), .shift(7'b0001100), .out(barrelshifter_15_out));
  Add #(.Bits(32)) add_1 (
    .a(_32_bit_cla_9_s), .b(barrelshifter_13_out), .c_i(_32_bit_cla_9_c_out), .s(add_1_s));  // open: c_o
  Add #(.Bits(32)) add_2 (.a(add_1_s), .b(barrelshifter_14_out), .c_i(_32_bit_cla_10_c_out), .s(add_2_s));  // open: c_o
  Add #(.Bits(32)) add_3 (.a(add_2_s), .b(barrelshifter_15_out), .c_i(_32_bit_cla_11_c_out), .s(P));  // open: c_o
endmodule
