// Digital circuit pre_post_addr.dig as structural Verilog
module pre_post_addr (
  input  [15:0] RA,
  input  [15:0] RB,
  input  en,
  output [15:0] _1A
);

  wire [15:0] cla_1_s;

  Multiplexer #(.Bits(16)) multiplexer_1 (.sel(en), .in_0(cla_1_s), .in_1(RA), .out(_1A));
  CLA cla_1 (.A(RA), .B(RB), .C_in(1'b0), .S(cla_1_s));  // open: C_out
endmodule
