// Digital circuit reg_file.dig as structural Verilog
module reg_file (
  input  [2:0] RS1,
  input  [2:0] RS2,
  input  [2:0] WS,
  input  WE,
  input  [15:0] IN,
  input  CLK,
  input  [15:0] FLAG,
  input  FLEN,
  output [15:0] OUT1,
  output [15:0] OUT2,
  output [15:0] PC,
  output [15:0] RD,
  output [15:0] FL_out
);

  wire and_1_out, and_2_out, and_3_out, and_4_out, and_5_out, and_6_out, decoder_1_out_0, decoder_1_out_1,
       decoder_1_out_2, decoder_1_out_3, decoder_1_out_4, decoder_1_out_5, decoder_1_out_6,
       multiplexer_1_out, or_1_out;
  wire [15:0] counter_1_q, multiplexer_2_out, R1_q, R2_q, R3_q, R4_q;

  Decoder #(.Selector_Bits(3)) decoder_1 (
    .sel(WS), .out_0(decoder_1_out_0), .out_1(decoder_1_out_1), .out_2(decoder_1_out_2),
    .out_3(decoder_1_out_3), .out_4(decoder_1_out_4), .out_5(decoder_1_out_5), .out_6(decoder_1_out_6));  // open: out_7
  and and_1 (and_1_out, decoder_1_out_0, WE);
  and and_2 (and_2_out, decoder_1_out_1, WE);
  and and_3 (and_3_out, decoder_1_out_2, WE);
  and and_4 (and_4_out, decoder_1_out_3, WE);
  and and_5 (and_5_out, decoder_1_out_4, WE);
  or or_1 (or_1_out, decoder_1_out_5, FLEN);
  and and_6 (and_6_out, WE, decoder_1_out_6);
  Multiplexer multiplexer_1 (.sel(and_6_out), .in_0(1'b1), .in_1(and_6_out), .out(multiplexer_1_out));
  Multiplexer #(.Bits(16)) multiplexer_2 (.sel(and_6_out), .in_0(counter_1_q), .in_1(IN), .out(multiplexer_2_out));
  Register #(.Bits(16)) RZ (.D(IN), .C(CLK), .en(and_1_out));  // open: Q
  Register #(.Bits(16)) R1 (.D(IN), .C(CLK), .en(and_2_out), .Q(R1_q));
  Register #(.Bits(16)) R2 (.D(IN), .C(CLK), .en(and_3_out), .Q(R2_q));
  Register #(.Bits(16)) R3 (.D(IN), .C(CLK), .en(and_4_out), .Q(R3_q));
  Register #(.Bits(16)) R4 (.D(IN), .C(CLK), .en(and_5_out), .Q(R4_q));
  Register #(.Bits(16)) FL (.D(FLAG), .C(CLK), .en(or_1_out), .Q(FL_out));
  counter counter_1 (.PC(PC), .Q(counter_1_q));
  Register #(.Bits(16), .isProgramCounter("true")) u_PC (
    .D(multiplexer_2_out), .C(CLK), .en(multiplexer_1_out), .Q(PC));
  Multiplexer #(.Selector_Bits(3), .Bits(16)) multiplexer_3 (
    .sel(RS1), .in_0({16{1'b0}}), .in_1(R1_q), .in_2(R2_q), .in_3(R3_q), .in_4(R4_q), .in_5(FL_out),
    .in_6(PC), .in_7({16{1'b0}}), .out(OUT1));
  Multiplexer #(.Selector_Bits(3), .Bits(16)) multiplexer_4 (
    .sel(RS2), .in_0({16{1'b0}}), .in_1(R1_q), .in_2(R2_q), .in_3(R3_q), .in_4(R4_q), .in_5(FL_out),
    .in_6(PC), .in_7({16{1'b0}}), .out(OUT2));
  Multiplexer #(.Selector_Bits(3), .Bits(16)) multiplexer_5 (
    .sel(WS), .in_0({16{1'b0}}), .in_1(R1_q), .in_2(R2_q), .in_3(R3_q), .in_4(R4_q), .in_5(FL_out),
    .in_6(PC), .in_7({16{1'b0}}), .out(RD));

  // Notes on the sheet:
  //   RS1: The index of the register which should output its value to OUT1.
  //   RS2: The index of the register which should output its value to OUT2.
  //   WS: The index of the register which should save the value on IN on the next clock cycle (if WE is high).
  //   WE: Whether the register selected by WS should save the value from IN on the next cycle.
  //   IN: The value to be saved into the register specified by WS if WE is high,
  //   OUT1: The value in the register specified by RS1.
  //   OUT2: The value in the register specified by RS2.
  //   PC: The value in the register specified by RS2.
  //   RD: The value in the register specified by RS2.
  //   FL_out: The value in the register specified by RS2.
endmodule

/* Test case:
CLK RS1 RS2 WS WE IN OUT1 OUT2
c 0 0 0 1 0x1234 0x0000 0x0000
c 1 0 1 1 0xBEEF 0xBEEF 0x0000
c 2 1 2 1 0xDEAD 0xDEAD 0xBEEF
c 3 2 3 1 0xFFFF 0xFFFF 0xDEAD
c 3 2 3 0 0xABCD 0xFFFF 0xDEAD
c 3 2 2 0 0xABCD 0xFFFF 0xDEAD
c 1 0 1 0 0xABCD 0xBEEF 0x0000
c 1 0 0 0 0xABCD 0xBEEF 0x0000
c 1 0 2 1 0xBADE 0xBEEF 0x0000
c 0 2 2 1 0xBADE 0x0000 0xBADE
c 0 0 2 0 0x1234 0x0000 0x0000
c 2 3 0 1 0x0000 0xBADE 0xFFFF
c 0 0 2 0 0x1234 0x0000 0x0000
*/
