// Digital circuit reg_file_extn.dig as structural Verilog
module reg_file_extn (
  input  [2:0] RS1,
  input  [2:0] RS2,
  input  [2:0] WS1,
  input  WE,
  input  [15:0] D_IN1,
  input  CLK,
  input  [15:0] FLAG,
  input  FLEN,
  input  [2:0] WS2,
  input  [15:0] D_IN2,
  input  [2:0] RS3,
  input  SHADOW_en,
  output [15:0] OUT1,
  output [15:0] OUT2,
  output [15:0] PC,
  output [15:0] OUT3,
  output [15:0] FL
);

  wire and_1_out, and_2_out, and_3_out, and_4_out, and_5_out, and_6_out, and_7_out, and_8_out, and_9_out,
       and_10_out, and_11_out, and_12_out, and_13_out, and_14_out, decoder_1_out_0, decoder_1_out_1,
       decoder_1_out_2, decoder_1_out_3, decoder_1_out_4, decoder_1_out_5, decoder_1_out_6, decoder_1_out_7,
       decoder_2_out_0, decoder_2_out_1, decoder_2_out_2, decoder_2_out_3, decoder_2_out_4, decoder_2_out_6,
       decoder_2_out_7, demultiplexer_1_out_0, demultiplexer_1_out_1, demultiplexer_2_out_0,
       demultiplexer_2_out_1, demultiplexer_3_out_0, demultiplexer_3_out_1, demultiplexer_4_out_0,
       demultiplexer_4_out_1, multiplexer_8_out, or_1_out, or_2_out, or_3_out, or_4_out, or_5_out, or_6_out,
       or_7_out, or_8_out;
  wire [15:0] counter_1_q, multiplexer_1_out, multiplexer_2_out, multiplexer_3_out, multiplexer_4_out,
       multiplexer_5_out, multiplexer_6_out, multiplexer_7_out, multiplexer_9_out, multiplexer_10_out,
       multiplexer_11_out, multiplexer_12_out, multiplexer_13_out, OFFSET_q, R1_q, R2_q, R3_q, R4_q,
       SHADOW_R1_q, SHADOW_R2_q, SHADOW_R3_q, SHADOW_R4_q;

  Decoder #(.Selector_Bits(3)) decoder_1 (
    .sel(WS1), .out_0(decoder_1_out_0), .out_1(decoder_1_out_1), .out_2(decoder_1_out_2),
    .out_3(decoder_1_out_3), .out_4(decoder_1_out_4), .out_5(decoder_1_out_5), .out_6(decoder_1_out_6),
    .out_7(decoder_1_out_7));
  Decoder #(.Selector_Bits(3)) decoder_2 (
    .sel(WS2), .out_0(decoder_2_out_0), .out_1(decoder_2_out_1), .out_2(decoder_2_out_2),
    .out_3(decoder_2_out_3), .out_4(decoder_2_out_4), .out_6(decoder_2_out_6), .out_7(decoder_2_out_7));  // open: out_5
  and and_1 (and_1_out, decoder_2_out_0, WE);
  and and_2 (and_2_out, decoder_2_out_1, WE);
  and and_3 (and_3_out, decoder_2_out_2, WE);
  and and_4 (and_4_out, decoder_2_out_3, WE);
  and and_5 (and_5_out, decoder_2_out_4, WE);
  and and_6 (and_6_out, decoder_2_out_6, WE);
  and and_7 (and_7_out, decoder_2_out_7, WE);
  and and_8 (and_8_out, decoder_1_out_0, WE);
  and and_9 (and_9_out, decoder_1_out_1, WE);
  and and_10 (and_10_out, decoder_1_out_2, WE);
  and and_11 (and_11_out, decoder_1_out_3, WE);
  and and_12 (and_12_out, decoder_1_out_4, WE);
  and and_13 (and_13_out, WE, decoder_1_out_6);
  and and_14 (and_14_out, WE, decoder_1_out_7);
  or or_1 (or_1_out, and_8_out, and_1_out);
  or or_2 (or_2_out, and_9_out, and_2_out);
  or or_3 (or_3_out, and_10_out, and_3_out);
  or or_4 (or_4_out, and_11_out, and_4_out);
  or or_5 (or_5_out, and_12_out, and_5_out);
  or or_6 (or_6_out, and_13_out, and_6_out);
  or or_7 (or_7_out, and_14_out, and_7_out);
  or or_8 (or_8_out, decoder_1_out_5, FLEN);
  Multiplexer #(.Bits(16)) multiplexer_1 (.sel(and_8_out), .in_0(D_IN2), .in_1(D_IN1), .out(multiplexer_1_out));
  Multiplexer #(.Bits(16)) multiplexer_2 (.sel(and_9_out), .in_0(D_IN2), .in_1(D_IN1), .out(multiplexer_2_out));
  Multiplexer #(.Bits(16)) multiplexer_3 (.sel(and_10_out), .in_0(D_IN2), .in_1(D_IN1), .out(multiplexer_3_out));
  Multiplexer #(.Bits(16)) multiplexer_4 (.sel(and_11_out), .in_0(D_IN2), .in_1(D_IN1), .out(multiplexer_4_out));
  Multiplexer #(.Bits(16)) multiplexer_5 (.sel(and_12_out), .in_0(D_IN2), .in_1(D_IN1), .out(multiplexer_5_out));
  Multiplexer #(.Bits(16)) multiplexer_6 (.sel(and_13_out), .in_0(D_IN1), .in_1(D_IN2), .out(multiplexer_6_out));
  Multiplexer #(.Bits(16)) multiplexer_7 (.sel(and_14_out), .in_0(D_IN1), .in_1(D_IN2), .out(multiplexer_7_out));
  Multiplexer multiplexer_8 (.sel(or_6_out), .in_0(1'b1), .in_1(or_6_out), .out(multiplexer_8_out));
  Demultiplexer demultiplexer_1 (
    .sel(SHADOW_en), .in(or_2_out), .out_0(demultiplexer_1_out_0), .out_1(demultiplexer_1_out_1));
  Demultiplexer demultiplexer_2 (
    .sel(SHADOW_en), .in(or_3_out), .out_0(demultiplexer_2_out_0), .out_1(demultiplexer_2_out_1));
  Demultiplexer demultiplexer_3 (
    .sel(SHADOW_en), .in(or_4_out), .out_0(demultiplexer_3_out_0), .out_1(demultiplexer_3_out_1));
  Demultiplexer demultiplexer_4 (
    .sel(SHADOW_en), .in(or_5_out), .out_0(demultiplexer_4_out_0), .out_1(demultiplexer_4_out_1));
  Multiplexer #(.Bits(16)) multiplexer_9 (
    .sel(or_6_out), .in_0(counter_1_q), .in_1(multiplexer_6_out), .out(multiplexer_9_out));
  Register #(.Bits(16)) RZ (.D(multiplexer_1_out), .C(CLK), .en(or_1_out));  // open: Q
  Register #(.Bits(16)) R1 (.D(multiplexer_2_out), .C(CLK), .en(demultiplexer_1_out_0), .Q(R1_q));
  Register #(.Bits(16)) R2 (.D(multiplexer_3_out), .C(CLK), .en(demultiplexer_2_out_0), .Q(R2_q));
  Register #(.Bits(16)) R3 (.D(multiplexer_4_out), .C(CLK), .en(demultiplexer_3_out_0), .Q(R3_q));
  Register #(.Bits(16)) R4 (.D(multiplexer_5_out), .C(CLK), .en(demultiplexer_4_out_0), .Q(R4_q));
  Register #(.Bits(16)) u_FL (.D(FLAG), .C(CLK), .en(or_8_out), .Q(FL));
  counter counter_1 (.PC(PC), .Q(counter_1_q));
  Register #(.Bits(16), .isProgramCounter("true")) u_PC (
    .D(multiplexer_9_out), .C(CLK), .en(multiplexer_8_out), .Q(PC));
  Register #(.Bits(16)) OFFSET (.D(multiplexer_7_out), .C(CLK), .en(or_7_out), .Q(OFFSET_q));
  Register #(.Bits(16)) SHADOW_R1 (.D(multiplexer_2_out), .C(CLK), .en(demultiplexer_1_out_1), .Q(SHADOW_R1_q));
  Register #(.Bits(16)) SHADOW_R2 (.D(multiplexer_3_out), .C(CLK), .en(demultiplexer_2_out_1), .Q(SHADOW_R2_q));
  Register #(.Bits(16)) SHADOW_R3 (.D(multiplexer_4_out), .C(CLK), .en(demultiplexer_3_out_1), .Q(SHADOW_R3_q));
  Register #(.Bits(16)) SHADOW_R4 (.D(multiplexer_5_out), .C(CLK), .en(demultiplexer_4_out_1), .Q(SHADOW_R4_q));
  Multiplexer #(.Bits(16)) multiplexer_10 (.sel(SHADOW_en), .in_0(R1_q), .in_1(SHADOW_R1_q), .out(multiplexer_10_out));
  Multiplexer #(.Bits(16)) multiplexer_11 (.sel(SHADOW_en), .in_0(R2_q), .in_1(SHADOW_R2_q), .out(multiplexer_11_out));
  Multiplexer #(.Bits(16)) multiplexer_12 (.sel(SHADOW_en), .in_0(R3_q), .in_1(SHADOW_R3_q), .out(multiplexer_12_out));
  Multiplexer #(.Bits(16)) multiplexer_13 (.sel(SHADOW_en), .in_0(R4_q), .in_1(SHADOW_R4_q), .out(multiplexer_13_out));
  Multiplexer #(.Selector_Bits(3), .Bits(16)) multiplexer_14 (
    .sel(RS1), .in_0({16{1'b0}}), .in_1(multiplexer_10_out), .in_2(multiplexer_11_out),
    .in_3(multiplexer_12_out), .in_4(multiplexer_13_out), .in_5(FL), .in_6(PC), .in_7(OFFSET_q), .out(OUT1));
  Multiplexer #(.Selector_Bits(3), .Bits(16)) multiplexer_15 (
    .sel(RS2), .in_0({16{1'b0}}), .in_1(multiplexer_10_out), .in_2(multiplexer_11_out),
    .in_3(multiplexer_12_out), .in_4(multiplexer_13_out), .in_5(FL), .in_6(PC), .in_7(OFFSET_q), .out(OUT2));
  Multiplexer #(.Selector_Bits(3), .Bits(16)) multiplexer_16 (
    .sel(RS3), .in_0({16{1'b0}}), .in_1(multiplexer_10_out), .in_2(multiplexer_11_out),
    .in_3(multiplexer_12_out), .in_4(multiplexer_13_out), .in_5(FL), .in_6(PC), .in_7(OFFSET_q), .out(OUT3));

  // Other names for the same wires on the sheet: SH_en = SHADOW_en; WS[2:0] = WS1

  // Notes on the sheet:
  //   RS1: The index of the register which should output its value to OUT1.
  //   RS2: The index of the register which should output its value to OUT2.
  //   WS1: The index of the register which should save the value on IN on the next clock cycle (if WE is high).
  //   WE: Whether the register selected by WS should save the value from IN on the next cycle.
  //   D_IN1: The value to be saved into the register specified by WS if WE is high,
  //   OUT1: The value in the register specified by RS1.
  //   OUT2: The value in the register specified by RS2.
  //   PC: The value in the register specified by RS2.
  //   OUT3: dest register
  //   WS2: The index of the register which should save the value on IN on the next clock cycle (if WE is high).
  //   D_IN2: The value to be saved into the register specified by WS if WE is high,
  //   RS3: The index of the register which should output its value to OUT2.
  //   SHADOW_en: Whether the register selected by WS should save the value from IN on the next cycle.
endmodule

/* Test case REG_FILE:
CLK RS1 RS2 WS1 WE D_IN1 OUT1 OUT2
c 0 0 0 1 0x1234 0x0000 0x0000
c 1 0 1 1 0xBEEF 0xBEEF 0x0000
c 2 1 2 1 0xDEAD 0xDEAD 0xBEEF
c 3 2 3 1 0xFFFF 0xFFFF 0xDEAD
c 3 2 3 0 0xABCD 0xFFFF 0xDEAD
c 3 2 2 0 0xABCD 0xFFFF 0xDEAD
c 1 0 1 0 0xABCD 0xBEEF 0x0000
c 1 0 0 0 0xABCD 0xBEEF 0x0000
c 1 0 2 1 0xBADE 0xBEEF 0x0000
c 0 2 2 1 0xBADE 0x0000 0xBADE
c 0 0 2 0 0x1234 0x0000 0x0000
c 2 3 0 1 0x0000 0xBADE 0xFFFF
c 0 0 2 0 0x1234 0x0000 0x0000
*/
