// Digital circuit seth.dig as structural Verilog
module seth (
  input  [15:0] IMM8,
  input  [15:0] RD,
  output [15:0] SETH
);

  wire [15:0] and_1_out, barrelshifter_1_out;

  BarrelShifter #(.Bits(16)) barrelshifter_1 (.in(IMM8), .shift(5'b01000), .out(barrelshifter_1_out));
  assign and_1_out = RD & 16'hff;  // And and_1, 16 bits wide
  assign SETH = barrelshifter_1_out | and_1_out;  // Or or_1, 16 bits wide
  // Pins of 1 and 16 bits meet at IMM8
endmodule
