// Digital circuit zero_comparator.dig as structural Verilog
module zero_comparator (
  input  [15:0] INST,
  output Z
);

  wire Zero_eq;

  Comparator #(.Bits(16)) Zero (.a(INST), .b({16{1'b0}}), .eq(Zero_eq));  // open: gt, lt
  and and_1 (Z, 1'b1, Zero_eq);
endmodule
